// Logisim project CPU_0.circ as structural Verilog: 29 circuits, main circuit main
module main (
  input  in_1,
  input  in_2,
  input  in_3,
  input  in_4,
  input  in_5,
  input  in_6,
  input  in_7,
  input  in_8,
  input  in_9,
  input  in_10,
  input  in_11,
  input  in_12,
  input  in_13,
  input  in_14
);

  wire C, CLK, D, N, RDY, V, Z;
  wire [3:0] microSeq_q0;
  wire [7:0] ADDR_H, ADDR_L, DATA, IR_q0, LHS, RHS;
  wire [15:0] ADDR, DECODE_ROM_data;
  wire [15:13] ALU_data;

  Clock clock_1 (.out(CLK));
  LED led_1 (.in(RDY));
  SHADOW_RAM MEMORY (.DATA_OUT(DATA), .RDY(RDY), .CLK(CLK), ._RAM_WRITE(in_1), .ADDR_IN(ADDR));
  ROM #(.addrWidth(21), .dataWidth(16)) ALU (
    .addr({in_12, in_11, in_10, in_9, in_8, RHS, LHS}), .data({ALU_data, C, V, Z, N, D, DATA}));
  _74574 u_ADDR_H (
    .Q0(ADDR_H[0]), .Q1(ADDR_H[1]), .Q2(ADDR_H[2]), .Q3(ADDR_H[3]), .Q4(ADDR_H[4]), .Q5(ADDR_H[5]),
    .Q6(ADDR_H[6]), .Q7(ADDR_H[7]), .VCC(RDY), ._OE(in_4), .CP(CLK), .D0(DATA[0]), .D1(DATA[1]),
    .D2(DATA[2]), .D3(DATA[3]), .D4(DATA[4]), .D5(DATA[5]), .D6(DATA[6]), .D7(DATA[7]), .GND(1'b0));
  _74574 IR (
    .Q0(IR_q0[0]), .Q1(IR_q0[1]), .Q2(IR_q0[2]), .Q3(IR_q0[3]), .Q4(IR_q0[4]), .Q5(IR_q0[5]), .Q6(IR_q0[6]),
    .Q7(IR_q0[7]), .VCC(RDY), ._OE(in_13), .CP(CLK), .D0(DATA[0]), .D1(DATA[1]), .D2(DATA[2]), .D3(DATA[3]),
    .D4(DATA[4]), .D5(DATA[5]), .D6(DATA[6]), .D7(DATA[7]), .GND(1'b0));
  _74163 microSeq (
    .Q0(microSeq_q0[0]), .Q1(microSeq_q0[1]), .Q2(microSeq_q0[2]), .Q3(microSeq_q0[3]), .CP(CLK), .D0(1'b0),
    .D1(1'b0), .D2(1'b0), .D3(1'b0), .ENP(1'b1), .GND(1'b0), ._CLR(in_14), .ENT(1'b1), ._LD(1'b1), .VCC(RDY));  // open: RCO
  _74574 u_ADDR_L (
    .Q0(ADDR_L[0]), .Q1(ADDR_L[1]), .Q2(ADDR_L[2]), .Q3(ADDR_L[3]), .Q4(ADDR_L[4]), .Q5(ADDR_L[5]),
    .Q6(ADDR_L[6]), .Q7(ADDR_L[7]), .VCC(RDY), ._OE(in_5), .CP(CLK), .D0(DATA[0]), .D1(DATA[1]),
    .D2(DATA[2]), .D3(DATA[3]), .D4(DATA[4]), .D5(DATA[5]), .D6(DATA[6]), .D7(DATA[7]), .GND(1'b0));
  ROM #(.addrWidth(16), .dataWidth(16)) DECODE_ROM (.addr({4'b0000, microSeq_q0, IR_q0}), .data(DECODE_ROM_data));
  _74574 A (
    .Q0(LHS[0]), .Q1(LHS[1]), .Q2(LHS[2]), .Q3(LHS[3]), .Q4(LHS[4]), .Q5(LHS[5]), .Q6(LHS[6]), .Q7(LHS[7]),
    .VCC(RDY), ._OE(in_2), .CP(CLK), .D0(DATA[0]), .D1(DATA[1]), .D2(DATA[2]), .D3(DATA[3]), .D4(DATA[4]),
    .D5(DATA[5]), .D6(DATA[6]), .D7(DATA[7]), .GND(1'b0));
  _74574 B (
    .Q0(RHS[0]), .Q1(RHS[1]), .Q2(RHS[2]), .Q3(RHS[3]), .Q4(RHS[4]), .Q5(RHS[5]), .Q6(RHS[6]), .Q7(RHS[7]),
    .VCC(RDY), ._OE(in_3), .CP(CLK), .D0(DATA[0]), .D1(DATA[1]), .D2(DATA[2]), .D3(DATA[3]), .D4(DATA[4]),
    .D5(DATA[5]), .D6(DATA[6]), .D7(DATA[7]), .GND(1'b0));

  // Other names for the same wires on the sheet: ALUOP_0 = in_8; ALUOP_1 = in_9; ALUOP_2 = in_10; ALUOP_3 = in_11;
  //   ALUOP_4 = in_12; _A_LOAD = in_2; _AH_LOAD = in_4; _AL_LOAD = in_5; _B_LOAD = in_3; _IR_LOAD = in_13;
  //   _PCH_LOAD = in_6; _PCL_LOAD = in_7; _RAM_W = in_1; _Seq_RST = in_14
endmodule

module _7400 (
  input  VCC,
  input  A0,
  input  B0,
  input  A1,
  input  B1,
  input  A2,
  input  B2,
  input  A3,
  input  B3,
  input  GND,
  output Y0,
  output Y1,
  output Y2,
  output Y3
);

  nand nand_1 (Y0, A0, B0);
  nand nand_2 (Y1, A1, B1);
  nand nand_3 (Y2, A2, B2);
  nand nand_4 (Y3, A3, B3);
endmodule

module _7402 (
  input  VCC,
  input  A0,
  input  B0,
  input  A1,
  input  B1,
  input  A2,
  input  B2,
  input  A3,
  input  B3,
  input  GND,
  output Y0,
  output Y1,
  output Y2,
  output Y3
);

  nor nor_1 (Y0, A0, B0);
  nor nor_2 (Y1, A1, B1);
  nor nor_3 (Y2, A2, B2);
  nor nor_4 (Y3, A3, B3);
endmodule

module _7404 (
  input  A0,
  input  VCC,
  input  A5,
  input  A1,
  input  A4,
  input  A2,
  input  A3,
  input  GND,
  output Y0,
  output Y5,
  output Y1,
  output Y4,
  output Y2,
  output Y3
);

  not not_1 (Y0, A0);
  not not_2 (Y1, A1);
  not not_3 (Y2, A2);
  not not_4 (Y5, A5);
  not not_5 (Y4, A4);
  not not_6 (Y3, A3);
endmodule

module _7408 (
  input  VCC,
  input  A0,
  input  B0,
  input  A1,
  input  B1,
  input  A2,
  input  B2,
  input  A3,
  input  B3,
  input  GND,
  output Y0,
  output Y1,
  output Y2,
  output Y3
);

  and and_1 (Y0, A0, B0);
  and and_2 (Y1, A1, B1);
  and and_3 (Y2, A2, B2);
  and and_4 (Y3, A3, B3);
endmodule

module _74138 (
  input  A,
  input  VCC,
  input  B,
  input  C,
  input  _EA,
  input  _EB,
  input  E,
  input  GND,
  output Y0,
  output Y1,
  output Y2,
  output Y3,
  output Y4,
  output Y7,
  output Y5,
  output Y6
);

  wire and_1_out, and_2_out, and_3_out, and_4_out, and_5_out, and_6_out, and_7_out, and_8_out, and_9_out,
       decoder_1_out0, decoder_1_out1, decoder_1_out2, decoder_1_out3, decoder_1_out4, decoder_1_out5,
       decoder_1_out6, decoder_1_out7, not_1_out, not_2_out;

  not not_1 (not_1_out, _EA);
  not not_2 (not_2_out, _EB);
  and and_1 (and_1_out, and_2_out, decoder_1_out7);
  not not_3 (Y7, and_1_out);
  and and_2 (and_2_out, not_1_out, not_2_out, E);
  Decoder #(.enable("false"), .select(3)) decoder_1 (
    .out0(decoder_1_out0), .out1(decoder_1_out1), .out2(decoder_1_out2), .out3(decoder_1_out3),
    .out4(decoder_1_out4), .out5(decoder_1_out5), .out6(decoder_1_out6), .out7(decoder_1_out7),
    .sel({C, B, A}));
  and and_3 (and_3_out, and_2_out, decoder_1_out0);
  not not_4 (Y0, and_3_out);
  and and_4 (and_4_out, and_2_out, decoder_1_out1);
  not not_5 (Y1, and_4_out);
  and and_5 (and_5_out, and_2_out, decoder_1_out2);
  not not_6 (Y2, and_5_out);
  and and_6 (and_6_out, and_2_out, decoder_1_out3);
  not not_7 (Y3, and_6_out);
  and and_7 (and_7_out, and_2_out, decoder_1_out4);
  not not_8 (Y4, and_7_out);
  and and_8 (and_8_out, and_2_out, decoder_1_out5);
  not not_9 (Y5, and_8_out);
  and and_9 (and_9_out, and_2_out, decoder_1_out6);
  not not_10 (Y6, and_9_out);
endmodule

module _74139 (
  input  _1__1G,
  input  _16__Vcc,
  input  _2__1A,
  input  _15__2G,
  input  _3__1B,
  input  _14__2A,
  input  _13__2B,
  input  _8__GND,
  output _4__1Y0,
  output _5__1Y1,
  output _12__2Y0,
  output _6__1Y2,
  output _11__2Y1,
  output _7__1Y3,
  output _10__2Y2,
  output _9__2Y3
);

  wire decoder_1_out0, decoder_1_out1, decoder_1_out2, decoder_1_out3, decoder_2_out0, decoder_2_out1,
       decoder_2_out2, decoder_2_out3, not_1_out, not_2_out, not_3_out, not_4_out, not_5_out, not_6_out,
       not_7_out, not_8_out, not_9_out, not_10_out;

  not not_1 (not_1_out, _1__1G);
  and and_1 (_4__1Y0, not_1_out, not_2_out);
  not not_2 (not_2_out, decoder_1_out0);
  and and_2 (_5__1Y1, not_1_out, not_3_out);
  not not_3 (not_3_out, decoder_1_out1);
  and and_3 (_6__1Y2, not_1_out, not_4_out);
  not not_4 (not_4_out, decoder_1_out2);
  and and_4 (_7__1Y3, not_1_out, not_5_out);
  not not_5 (not_5_out, decoder_1_out3);
  Decoder #(.enable("false"), .select(2)) decoder_1 (
    .out0(decoder_1_out0), .out1(decoder_1_out1), .out2(decoder_1_out2), .out3(decoder_1_out3),
    .sel({_3__1B, _2__1A}));
  Decoder #(.enable("false"), .select(2)) decoder_2 (
    .out0(decoder_2_out0), .out1(decoder_2_out1), .out2(decoder_2_out2), .out3(decoder_2_out3),
    .sel({_13__2B, _14__2A}));
  not not_6 (not_6_out, _15__2G);
  not not_7 (not_7_out, decoder_2_out0);
  not not_8 (not_8_out, decoder_2_out1);
  not not_9 (not_9_out, decoder_2_out2);
  not not_10 (not_10_out, decoder_2_out3);
  and and_5 (_12__2Y0, not_6_out, not_7_out);
  and and_6 (_11__2Y1, not_6_out, not_8_out);
  and and_7 (_10__2Y2, not_6_out, not_9_out);
  and and_8 (_9__2Y3, not_6_out, not_10_out);
endmodule

module _74151 (
  input  _1__D3,
  input  _16__Vcc,
  input  _2__D2,
  input  _15__D4,
  input  _3__D1,
  input  _14__D5,
  input  _4__D0,
  input  _13__D6,
  input  _12__D7,
  input  _11__A,
  input  _7__nG,
  input  _10__B,
  input  _8__GND,
  input  _9__C,
  output _5__Y,
  output _6__W
);

  wire multiplexer_1_out, not_2_out;

  not not_1 (_5__Y, _6__W);
  or or_1 (_6__W, not_2_out, _7__nG);
  not not_2 (not_2_out, multiplexer_1_out);
  Multiplexer #(.enable("false"), .select(3)) multiplexer_1 (
    .in0(_4__D0), .in1(_3__D1), .in2(_2__D2), .in3(_1__D3), .in4(_15__D4), .in5(_14__D5), .in6(_13__D6),
    .in7(_12__D7), .out(multiplexer_1_out), .sel({_9__C, _10__B, _11__A}));
endmodule

module _74157 (
  input  A1,
  input  B1,
  input  VCC,
  input  GND,
  input  A2,
  input  B2,
  input  A3,
  input  B3,
  input  A4,
  input  B4,
  input  S0,
  input  _OE,
  output Y1,
  output Y2,
  output Y3,
  output Y4
);

  wire and_1_out, and_2_out, and_3_out, and_4_out, and_5_out, and_6_out, and_7_out, and_8_out, not_1_out,
       not_2_out;

  not not_1 (not_1_out, S0);
  not not_2 (not_2_out, _OE);
  and and_1 (and_1_out, A1, not_1_out, not_2_out);
  and and_2 (and_2_out, B1, S0, not_2_out);
  and and_3 (and_3_out, A2, not_1_out, not_2_out);
  and and_4 (and_4_out, B2, S0, not_2_out);
  and and_5 (and_5_out, A3, not_1_out, not_2_out);
  and and_6 (and_6_out, B3, S0, not_2_out);
  and and_7 (and_7_out, A4, not_1_out, not_2_out);
  and and_8 (and_8_out, B4, S0, not_2_out);
  or or_1 (Y1, and_1_out, and_2_out);
  or or_2 (Y2, and_3_out, and_4_out);
  or or_3 (Y3, and_5_out, and_6_out);
  or or_4 (Y4, and_7_out, and_8_out);
endmodule

module _74163 (
  input  _CLR,
  input  VCC,
  input  CP,
  input  D0,
  input  D1,
  input  D2,
  input  D3,
  input  ENP,
  input  ENT,
  input  GND,
  input  _LD,
  output RCO,
  output Q0,
  output Q1,
  output Q2,
  output Q3
);

  wire and_1_out, and_2_out, counter_1_carry, not_1_out, not_2_out;
  wire [3:0] multiplexer_1_out;

  not not_1 (not_1_out, _CLR);
  Multiplexer #(.enable("false"), .width(4)) multiplexer_1 (
    .in0({D3, D2, D1, D0}), .in1(4'b0000), .out(multiplexer_1_out), .sel(not_1_out));
  and and_1 (and_1_out, ENP, and_2_out, ENT);
  Counter #(.max('hf), .width(4)) counter_1 (
    .load(not_2_out), .D(multiplexer_1_out), .count(and_1_out), .Q({Q3, Q2, Q1, Q0}),
    .carry(counter_1_carry), .clk(CP));  // open: clr
  not not_2 (not_2_out, and_2_out);
  and and_2 (and_2_out, ~not_1_out, _LD);  // AND_Gate
  and and_3 (RCO, counter_1_carry, ENT);
endmodule

module _74193 (
  input  D0,
  input  D1,
  input  D2,
  input  D3,
  input  _LD,
  input  UP,
  input  DN,
  input  CLR,
  input  VCC,
  input  GND,
  output _CO,
  output _BO,
  output Q0,
  output Q1,
  output Q2,
  output Q3
);

  wire and_1_out, and_2_out, and_3_out, and_4_out, and_5_out, and_6_out, buffer_1_out, buffer_2_out,
       buffer_3_out, buffer_5_out, buffer_7_out, buffer_9_out, nand_1_out, nand_2_out, nand_3_out,
       nand_4_out, nand_5_out, nand_6_out, nand_7_out, nand_8_out, nand_9_out, nand_10_out, nor_1_out,
       nor_2_out, nor_3_out, nor_4_out, not_1_out, not_2_out, not_3_out, not_4_out, not_5_out, not_6_out,
       not_7_out, not_8_out, not_9_out, or_1_out, or_2_out, or_3_out, or_4_out, or_5_out, t_ff_1_q,
       t_ff_1_qn, t_ff_2_q, t_ff_2_qn, t_ff_3_q, t_ff_3_qn, t_ff_4_q, t_ff_4_qn;

  not not_1 (not_1_out, VCC);
  not not_2 (not_2_out, _LD);
  not not_3 (not_3_out, UP);
  not not_4 (not_4_out, DN);
  or or_1 (or_1_out, CLR, not_1_out);
  not not_5 (not_5_out, or_1_out);
  buf buffer_1 (buffer_1_out, not_3_out);
  buf buffer_2 (buffer_2_out, not_4_out);
  buf buffer_3 (buffer_3_out, D0);
  nand nand_1 (nand_1_out, not_2_out, buffer_3_out);
  nand nand_2 (nand_2_out, nand_1_out, not_2_out);
  not not_6 (not_6_out, nand_1_out);
  T_Flip_Flop t_ff_1 (
    .clk(nor_1_out), .T(nor_1_out), .Q(t_ff_1_q), .Qn(t_ff_1_qn), .preset(not_6_out), .reset(or_2_out));
  nor nor_1 (nor_1_out, buffer_1_out, buffer_2_out);
  or or_2 (or_2_out, ~not_5_out, ~nand_2_out);  // OR_Gate
  buf buffer_4 (Q0, t_ff_1_q);
  and and_1 (and_1_out, not_3_out, t_ff_1_q);
  and and_2 (and_2_out, t_ff_1_qn, not_4_out);
  nand nand_3 (nand_3_out, not_2_out, buffer_5_out);
  not not_7 (not_7_out, nand_3_out);
  nor nor_2 (nor_2_out, and_1_out, and_2_out);
  buf buffer_5 (buffer_5_out, D1);
  nand nand_4 (nand_4_out, nand_3_out, not_2_out);
  T_Flip_Flop t_ff_2 (
    .clk(nor_2_out), .T(nor_2_out), .Q(t_ff_2_q), .Qn(t_ff_2_qn), .preset(not_7_out), .reset(or_3_out));
  or or_3 (or_3_out, ~not_5_out, ~nand_4_out);  // OR_Gate
  buf buffer_6 (Q1, t_ff_2_q);
  and and_3 (and_3_out, not_3_out, t_ff_1_q, t_ff_2_q);
  and and_4 (and_4_out, t_ff_2_qn, t_ff_1_qn, not_4_out);
  buf buffer_7 (buffer_7_out, D2);
  nand nand_5 (nand_5_out, not_2_out, buffer_7_out);
  not not_8 (not_8_out, nand_5_out);
  nor nor_3 (nor_3_out, and_3_out, and_4_out);
  nand nand_6 (nand_6_out, nand_5_out, not_2_out);
  T_Flip_Flop t_ff_3 (
    .clk(nor_3_out), .T(nor_3_out), .Q(t_ff_3_q), .Qn(t_ff_3_qn), .preset(not_8_out), .reset(or_4_out));
  or or_4 (or_4_out, ~not_5_out, ~nand_6_out);  // OR_Gate
  buf buffer_8 (Q2, t_ff_3_q);
  and and_5 (and_5_out, t_ff_2_q, not_3_out, t_ff_1_q, t_ff_3_q);
  and and_6 (and_6_out, t_ff_3_qn, t_ff_2_qn, t_ff_1_qn, not_4_out);
  nor nor_4 (nor_4_out, and_5_out, and_6_out);
  buf buffer_9 (buffer_9_out, D3);
  nand nand_7 (nand_7_out, not_2_out, buffer_9_out);
  nand nand_8 (nand_8_out, nand_7_out, not_2_out);
  not not_9 (not_9_out, nand_7_out);
  T_Flip_Flop t_ff_4 (
    .clk(nor_4_out), .T(nor_4_out), .Q(t_ff_4_q), .Qn(t_ff_4_qn), .preset(not_9_out), .reset(or_5_out));
  or or_5 (or_5_out, ~not_5_out, ~nand_8_out);  // OR_Gate
  buf buffer_10 (Q3, t_ff_4_q);
  nand nand_9 (nand_9_out, t_ff_3_q, not_3_out, t_ff_4_q, t_ff_2_q, t_ff_1_q);
  buf buffer_11 (_CO, nand_9_out);
  nand nand_10 (nand_10_out, t_ff_1_qn, t_ff_4_qn, t_ff_3_qn, t_ff_2_qn, not_4_out);
  buf buffer_12 (_BO, nand_10_out);
endmodule

module _74283 (
  input  CIN,
  input  VCC,
  input  A1,
  input  B1,
  input  GND,
  input  A2,
  input  B2,
  input  A3,
  input  B3,
  input  A4,
  input  B4,
  output Y1,
  output Y2,
  output Y3,
  output Y4,
  output COUT
);

  wire and_1_out, and_2_out, and_3_out, and_4_out, and_5_out, and_6_out, and_7_out, and_8_out, and_9_out,
       and_10_out, and_11_out, and_12_out, and_13_out, and_14_out, nand_1_out, nand_2_out, nand_3_out,
       nand_4_out, nor_1_out, nor_2_out, nor_3_out, nor_4_out, nor_5_out, nor_6_out, nor_7_out, not_1_out,
       not_2_out, not_3_out, not_4_out, not_5_out, not_6_out;

  not not_1 (not_1_out, CIN);
  nor nor_1 (nor_1_out, A1, B1);
  nand nand_1 (nand_1_out, A1, B1);
  nor nor_2 (nor_2_out, A2, B2);
  nand nand_2 (nand_2_out, A2, B2);
  nor nor_3 (nor_3_out, A3, B3);
  nand nand_3 (nand_3_out, A3, B3);
  nor nor_4 (nor_4_out, A4, B4);
  nand nand_4 (nand_4_out, A4, B4);
  not not_2 (not_2_out, not_1_out);
  not not_3 (not_3_out, nor_1_out);
  and and_1 (and_1_out, not_1_out, nand_1_out);
  not not_4 (not_4_out, nor_2_out);
  and and_2 (and_2_out, not_1_out, nand_1_out, nand_2_out);
  and and_3 (and_3_out, nand_2_out, nor_1_out);
  not not_5 (not_5_out, nor_3_out);
  and and_4 (and_4_out, not_1_out, nand_1_out, nand_2_out, nand_3_out);
  and and_5 (and_5_out, nand_2_out, nand_3_out, nor_1_out);
  and and_6 (and_6_out, nand_3_out, nor_2_out);
  not not_6 (not_6_out, nor_4_out);
  and and_7 (and_7_out, nand_1_out, nand_3_out);
  and and_8 (and_8_out, nand_2_out, nand_3_out, nand_4_out, nor_1_out);
  and and_9 (and_9_out, nand_3_out, nand_4_out, nor_2_out);
  and and_10 (and_10_out, nand_4_out, nor_3_out);
  and and_11 (and_11_out, not_3_out, nand_1_out);
  nor nor_5 (nor_5_out, and_1_out, nor_1_out);
  and and_12 (and_12_out, not_4_out, nand_2_out);
  nor nor_6 (nor_6_out, and_2_out, and_3_out, nor_2_out);
  and and_13 (and_13_out, not_5_out, nand_3_out);
  nor nor_7 (nor_7_out, and_4_out, and_5_out, and_6_out, nor_3_out);
  and and_14 (and_14_out, not_6_out, nand_4_out);
  nor nor_8 (COUT, and_8_out, and_10_out);
  xor xor_1 (Y1, not_2_out, and_11_out);
  xor xor_2 (Y2, nor_5_out, and_12_out);
  xor xor_3 (Y3, nor_6_out, and_13_out);
  xor xor_4 (Y4, nor_7_out, and_14_out);
endmodule

module _74541 (
  input  VCC,
  input  _E0,
  input  _E1,
  input  D0,
  input  D1,
  input  D2,
  input  D3,
  input  D4,
  input  D5,
  input  D6,
  input  D7,
  input  GND,
  output Q0,
  output Q1,
  output Q2,
  output Q3,
  output Q4,
  output Q5,
  output Q6,
  output Q7
);

  wire and_1_out, not_1_out, not_2_out;

  not not_1 (not_1_out, _E0);
  not not_2 (not_2_out, _E1);
  and and_1 (and_1_out, not_1_out, not_2_out);
  assign Q0 = and_1_out ? D0 : 1'bz;  // Controlled_Buffer controlled_buffer_1
  assign Q1 = and_1_out ? D1 : 1'bz;  // Controlled_Buffer controlled_buffer_2
  assign Q2 = and_1_out ? D2 : 1'bz;  // Controlled_Buffer controlled_buffer_3
  assign Q3 = and_1_out ? D3 : 1'bz;  // Controlled_Buffer controlled_buffer_4
  assign Q4 = and_1_out ? D4 : 1'bz;  // Controlled_Buffer controlled_buffer_5
  assign Q5 = and_1_out ? D5 : 1'bz;  // Controlled_Buffer controlled_buffer_6
  assign Q6 = and_1_out ? D6 : 1'bz;  // Controlled_Buffer controlled_buffer_7
  assign Q7 = and_1_out ? D7 : 1'bz;  // Controlled_Buffer controlled_buffer_8
endmodule

module _74574 (
  input  VCC,
  input  _OE,
  input  CP,
  input  D0,
  input  D1,
  input  D2,
  input  D3,
  input  D4,
  input  D5,
  input  D6,
  input  D7,
  input  GND,
  output Q0,
  output Q1,
  output Q2,
  output Q3,
  output Q4,
  output Q5,
  output Q6,
  output Q7
);

  wire and_1_out, d_ff_1_q, d_ff_2_q, d_ff_3_q, d_ff_4_q, d_ff_5_q, d_ff_6_q, d_ff_7_q, d_ff_8_q, not_1_out;

  not not_1 (not_1_out, _OE);
  and and_1 (and_1_out, VCC, not_1_out);
  D_Flip_Flop d_ff_1 (.clk(CP), .D(D0), .Q(d_ff_1_q));  // open: Qn, preset, reset
  D_Flip_Flop d_ff_2 (.clk(CP), .D(D1), .Q(d_ff_2_q));  // open: Qn, preset, reset
  D_Flip_Flop d_ff_3 (.clk(CP), .D(D2), .Q(d_ff_3_q));  // open: Qn, preset, reset
  D_Flip_Flop d_ff_4 (.clk(CP), .D(D3), .Q(d_ff_4_q));  // open: Qn, preset, reset
  D_Flip_Flop d_ff_5 (.clk(CP), .D(D4), .Q(d_ff_5_q));  // open: Qn, preset, reset
  D_Flip_Flop d_ff_6 (.clk(CP), .D(D5), .Q(d_ff_6_q));  // open: Qn, preset, reset
  D_Flip_Flop d_ff_7 (.clk(CP), .D(D6), .Q(d_ff_7_q));  // open: Qn, preset, reset
  D_Flip_Flop d_ff_8 (.clk(CP), .D(D7), .Q(d_ff_8_q));  // open: Qn, preset, reset
  assign Q0 = and_1_out ? d_ff_1_q : 1'bz;  // Controlled_Buffer controlled_buffer_1
  assign Q1 = and_1_out ? d_ff_2_q : 1'bz;  // Controlled_Buffer controlled_buffer_2
  assign Q2 = and_1_out ? d_ff_3_q : 1'bz;  // Controlled_Buffer controlled_buffer_3
  assign Q3 = and_1_out ? d_ff_4_q : 1'bz;  // Controlled_Buffer controlled_buffer_4
  assign Q4 = and_1_out ? d_ff_5_q : 1'bz;  // Controlled_Buffer controlled_buffer_5
  assign Q5 = and_1_out ? d_ff_6_q : 1'bz;  // Controlled_Buffer controlled_buffer_6
  assign Q6 = and_1_out ? d_ff_7_q : 1'bz;  // Controlled_Buffer controlled_buffer_7
  assign Q7 = and_1_out ? d_ff_8_q : 1'bz;  // Controlled_Buffer controlled_buffer_8
endmodule

module INT_REG (
  input  CLR,
  input  [7:0] LHS_IN,
  input  DEC,
  input  INC,
  input  _L,
  input  _INT_RST,
  input  _INT_TRIG,
  input  _A_L,
  input  _A_ADDR,
  input  CP,
  output [7:0] ADDR,
  output [7:0] LHS,
  output LED_OUTPUTS,
  output out_14,
  output out_15,
  output out_16,
  output out_17,
  output out_18,
  output out_19,
  output out_20
);

  wire D0, D1, D2, D3, D4, D5, D6, D7, n7400_1_y0, n7400_1_y1, n7400_1_y2, n7400_1_y3, n74193_1__bo,
       n74193_1__co, not_1_out, S0, S1, S2, S3, S4, S5, S6, S7;

  _7400 u_7400_1 (
    .Y0(n7400_1_y0), .Y1(n7400_1_y1), .Y2(n7400_1_y2), .Y3(n7400_1_y3), .A0(_INT_RST), .B0(_INT_TRIG),
    .A1(n7400_1_y0), .B1(n7400_1_y0), .A2(_L), .B2(n7400_1_y1), .A3(n7400_1_y2), .B3(n7400_1_y2), .GND(1'b0),
    .VCC(1'b1));
  _74574 u_74574_1 (
    .Q0(S0), .Q1(S1), .Q2(S2), .Q3(S3), .Q4(S4), .Q5(S5), .Q6(S6), .Q7(S7), .VCC(1'b1), ._OE(1'b0),
    .CP(not_1_out), .D0(LED_OUTPUTS), .D1(out_14), .D2(out_15), .D3(out_16), .D4(out_17), .D5(out_18),
    .D6(out_19), .D7(out_20), .GND(1'b0));
  not not_1 (not_1_out, _INT_TRIG);
  _74193 u_74193_1 (
    .Q3(out_16), ._CO(n74193_1__co), ._BO(n74193_1__bo), .Q0(LED_OUTPUTS), .Q1(out_14), .Q2(out_15), .D3(D3),
    .VCC(1'b1), .CLR(CLR), ._LD(n7400_1_y3), .UP(INC), .DN(DEC), .GND(1'b0), .D0(D0), .D1(D1), .D2(D2));
  _74574 u_74574_2 (
    .Q0(LHS[0]), .Q1(LHS[1]), .Q2(LHS[2]), .Q3(LHS[3]), .Q4(LHS[4]), .Q5(LHS[5]), .Q6(LHS[6]), .Q7(LHS[7]),
    .VCC(1'b1), ._OE(_A_L), .CP(CP), .D0(LED_OUTPUTS), .D1(out_14), .D2(out_15), .D3(out_16), .D4(out_17),
    .D5(out_18), .D6(out_19), .D7(out_20), .GND(1'b0));
  _74193 u_74193_2 (
    .Q3(out_20), .Q0(out_17), .Q1(out_18), .Q2(out_19), .D3(D7), .VCC(1'b1), .CLR(CLR), ._LD(n7400_1_y3),
    .UP(n74193_1__co), .DN(n74193_1__bo), .GND(1'b0), .D0(D4), .D1(D5), .D2(D6));  // open: _CO, _BO
  _74574 u_74574_3 (
    .Q0(ADDR[0]), .Q1(ADDR[1]), .Q2(ADDR[2]), .Q3(ADDR[3]), .Q4(ADDR[4]), .Q5(ADDR[5]), .Q6(ADDR[6]),
    .Q7(ADDR[7]), .VCC(1'b1), ._OE(_A_ADDR), .CP(CP), .D0(LED_OUTPUTS), .D1(out_14), .D2(out_15),
    .D3(out_16), .D4(out_17), .D5(out_18), .D6(out_19), .D7(out_20), .GND(1'b0));
  _74541 u_74541_1 (
    .Q0(D0), .Q1(D1), .Q2(D2), .Q3(D3), .Q4(D4), .Q5(D5), .Q6(D6), .Q7(D7), ._E0(_L), ._E1(1'b0),
    .D0(LHS_IN[0]), .D1(LHS_IN[1]), .D2(LHS_IN[2]), .D3(LHS_IN[3]), .D4(LHS_IN[4]), .D5(LHS_IN[5]),
    .D6(LHS_IN[6]), .D7(LHS_IN[7]), .GND(1'b0), .VCC(1'b1));
  _74541 u_74541_2 (
    .Q0(D0), .Q1(D1), .Q2(D2), .Q3(D3), .Q4(D4), .Q5(D5), .Q6(D6), .Q7(D7), ._E0(_INT_RST), ._E1(1'b0),
    .D0(S0), .D1(S1), .D2(S2), .D3(S3), .D4(S4), .D5(S5), .D6(S6), .D7(S7), .GND(1'b0), .VCC(1'b1));
  _74541 u_74541_3 (
    .Q0(D0), .Q1(D1), .Q2(D2), .Q3(D3), .Q4(D4), .Q5(D5), .Q6(D6), .Q7(D7), ._E0(_INT_TRIG), ._E1(1'b0),
    .D0(1'b1), .D1(1'b0), .D2(1'b1), .D3(1'b0), .D4(1'b1), .D5(1'b0), .D6(1'b1), .D7(1'b0), .GND(1'b0),
    .VCC(1'b1));

  // Other names for the same wires on the sheet: A0 = ADDR[0]; A1 = ADDR[1]; A2 = ADDR[2]; A3 = ADDR[3]; A4 = ADDR[4];
  //   A5 = ADDR[5]; A6 = ADDR[6]; A7 = ADDR[7]; L0 = LHS[0]; L1 = LHS[1]; L2 = LHS[2]; L3 = LHS[3]; L4 = LHS[4];
  //   L5 = LHS[5]; L6 = LHS[6]; L7 = LHS[7]; L0_IN = LHS_IN[0]; L1_IN = LHS_IN[1]; L2_IN = LHS_IN[2];
  //   L3_IN = LHS_IN[3]; L4_IN = LHS_IN[4]; L5_IN = LHS_IN[5]; L6_IN = LHS_IN[6]; L7_IN = LHS_IN[7]; Q0 = LED_OUTPUTS;
  //   Q1 = out_14; Q2 = out_15; Q3 = out_16; Q4 = out_17; Q5 = out_18; Q6 = out_19; Q7 = out_20

  // Notes on the sheet:
  //   BUS OUTPUTS
  //   BUS INPUTS
  //   MAIN CIRCUIT
endmodule

module SHADOW_RAM (
  input  CLK,
  input  _RAM_WRITE,
  input  [15:0] ADDR_IN,
  output [7:0] DATA_OUT,
  output RDY
);

  wire CLK_t, n74193_1__bo, n74193_1__co, n74193_2__bo, n74193_2__co, n74193_3__bo, n74193_3__co, not_2_out,
       not_3_out, or_1_out, RAM_WRITE, RDY_t;
  wire [7:0] MONITOR_ROM_data;
  wire [14:0] COUNT;
  wire [15:0] ADDR;

  ROM #(.addrWidth(16)) MONITOR_ROM (.addr(ADDR), .data(MONITOR_ROM_data));
  and and_1 (CLK_t, CLK, RDY_t);
  not not_1 (RAM_WRITE, _RAM_WRITE);
  _74193 u_74193_1 (
    .Q3(COUNT[3]), ._CO(n74193_1__co), ._BO(n74193_1__bo), .Q0(COUNT[0]), .Q1(COUNT[1]), .Q2(COUNT[2]),
    .D3(1'b0), .VCC(1'b1), .CLR(1'b0), ._LD(1'b1), .UP(CLK), .DN(1'b1), .GND(1'b0), .D0(1'b0), .D1(1'b0),
    .D2(1'b0));
  _74193 u_74193_2 (
    .Q3(COUNT[7]), ._CO(n74193_2__co), ._BO(n74193_2__bo), .Q0(COUNT[4]), .Q1(COUNT[5]), .Q2(COUNT[6]),
    .D3(1'b0), .VCC(1'b1), .CLR(1'b0), ._LD(1'b1), .UP(n74193_1__co), .DN(n74193_1__bo), .GND(1'b0),
    .D0(1'b0), .D1(1'b0), .D2(1'b0));
  D_Flip_Flop d_ff_1 (.clk(RDY_t), .D(RDY_t), .Q(RDY));  // open: Qn, preset, reset
  _74193 u_74193_3 (
    .Q3(COUNT[11]), ._CO(n74193_3__co), ._BO(n74193_3__bo), .Q0(COUNT[8]), .Q1(COUNT[9]), .Q2(COUNT[10]),
    .D3(1'b0), .VCC(1'b1), .CLR(1'b0), ._LD(1'b1), .UP(n74193_2__co), .DN(n74193_2__bo), .GND(1'b0),
    .D0(1'b0), .D1(1'b0), .D2(1'b0));
  not not_2 (not_2_out, RAM_WRITE);
  or or_1 (or_1_out, CLK_t, CLK);
  _74193 u_74193_4 (
    .Q3(RDY_t), .Q0(COUNT[12]), .Q1(COUNT[13]), .Q2(COUNT[14]), .D3(1'b0), .VCC(1'b1), .CLR(1'b0),
    ._LD(1'b1), .UP(n74193_3__co), .DN(n74193_3__bo), .GND(1'b0), .D0(1'b0), .D1(1'b0), .D2(1'b0));  // open: _CO, _BO
  RAM #(.addrWidth(16), .databus("bidir")) RAM (.addr(ADDR), .data(DATA_OUT));  // open: we, oe, clk
  assign DATA_OUT = RAM_WRITE ? MONITOR_ROM_data : 8'bz;  // Controlled_Buffer controlled_buffer_1
  assign ADDR = not_3_out ? {1'b0, COUNT} : 16'bz;  // Controlled_Buffer _16
  not not_3 (not_3_out, RDY_t);
  assign ADDR = RDY_t ? ADDR_IN : 16'bz;  // Controlled_Buffer _16_2

  // Other names for the same wires on the sheet: COPY_CLK = CLK; Q0 = COUNT[0]; Q1 = COUNT[1]; Q2 = COUNT[2];
  //   Q3 = COUNT[3]; Q4 = COUNT[4]; Q5 = COUNT[5]; Q6 = COUNT[6]; Q7 = COUNT[7]; Q8 = COUNT[8]; Q9 = COUNT[9];
  //   Q10 = COUNT[10]; Q11 = COUNT[11]; Q12 = COUNT[12]; Q13 = COUNT[13]; Q14 = COUNT[14]; DATA[7:0] = DATA_OUT

  // Notes on the sheet:
  //   contents of MONITOR_ROM (hex, n*v repeats v):
  //   1 2 3 4 5 6 7 8 9 a b c d e f 10 11 12 13 14 15 16 17 18 19 1a 1b 1c 1d 1e 1f 20
endmodule

module CPU (
  input  in_1
);

  wire _A_LHS_WRITE, _A_RHS_WRITE, _ALU_DATA_WRITE, _AR_ADDR_WRITE, _ARhi_RHS_WRITE, _ARlo_LHS_WRITE,
       _B_LHS_WRITE, _B_RHS_WRITE, _C_LHS_WRITE, _C_RHS_WRITE, _MEMBRIDGE_DATA_WRITE, _MEMBRIDGE_MEM_WRITE,
       _PC_ADDR_WRITE, _PC_LRHS_READ, _RAM_MEM_WRITE, _RAM_WRITE, _SP_ADDR_WRITE, _SP_LRHS_READ, _TCU_RESET,
       A_DATA_READ, alu_card_1_out_7, alu_card_1_out_8, alu_card_1_out_9, alu_card_1_out_10,
       alu_card_1_out_11, alu_card_1_out_12, alu_card_1_out_13, alu_card_1_out_14, alu_card_1_out_15,
       alu_card_1_out_16, alu_card_1_out_17, alu_card_1_out_18, alu_card_1_out_19, alu_card_1_out_20,
       alu_card_1_out_21, alu_card_1_out_22, alu_card_1_out_23, ar_card_1_out_7, ar_card_1_out_8,
       ar_card_1_out_9, ar_card_1_out_13, ar_card_1_out_14, ar_card_1_out_15, ar_card_1_out_16,
       ar_card_1_out_17, ar_card_1_out_18, ar_card_1_out_19, ar_card_1_out_20, ar_card_1_out_21,
       ar_card_1_out_22, ar_card_1_out_23, ar_card_1_out_24, ar_card_1_out_25, ar_card_1_out_26,
       ar_card_1_out_27, ar_card_1_out_28, AR_MEM_READ_hi, AR_MEM_READ_lo, B_DATA_READ,
       bus_controller_1_out_2, bus_controller_1_out_4, bus_controller_1_out_6, bus_controller_1_out_8,
       bus_controller_1_out_10, bus_controller_1_out_12, bus_controller_1_out_14, bus_controller_1_out_16,
       bus_controller_1_out_18, bus_controller_1_out_20, bus_controller_1_out_23, bus_controller_1_out_25,
       bus_controller_1_out_27, bus_controller_1_out_28, bus_controller_1_out_31, bus_controller_1_out_33,
       bus_controller_1_out_34, bus_controller_1_out_37, bus_controller_1_out_38, bus_controller_1_out_40,
       bus_controller_1_out_43, bus_controller_1_out_44, bus_controller_1_out_47, bus_controller_1_out_48,
       bus_controller_1_out_50, C_DATA_READ, CLK, gpr_card_1_out_5, gpr_card_1_out_6, gpr_card_1_out_7,
       gpr_card_1_out_10, gpr_card_1_out_11, gpr_card_1_out_12, gpr_card_1_out_13, gpr_card_1_out_14,
       gpr_card_1_out_15, gpr_card_1_out_16, gpr_card_1_out_17, gpr_card_2_out_5, gpr_card_2_out_6,
       gpr_card_2_out_7, gpr_card_2_out_10, gpr_card_2_out_11, gpr_card_2_out_12, gpr_card_2_out_13,
       gpr_card_2_out_14, gpr_card_2_out_15, gpr_card_2_out_16, gpr_card_2_out_17, gpr_card_3_out_5,
       gpr_card_3_out_6, gpr_card_3_out_7, gpr_card_3_out_10, gpr_card_3_out_11, gpr_card_3_out_12,
       gpr_card_3_out_13, gpr_card_3_out_14, gpr_card_3_out_15, gpr_card_3_out_16, gpr_card_3_out_17,
       ir_1_out_3, ir_1_out_4, ir_1_out_5, ir_1_out_6, ir_1_out_7, ir_1_out_9, ir_1_out_10, ir_1_out_11,
       IR_MEM_READ, membridge_1_out_5, membridge_1_out_6, memory_1_out_5, memory_1_out_6, memory_1_out_7,
       memory_1_out_8, memory_1_out_9, memory_1_out_10, memory_1_out_11, memory_1_out_12, pc_1_out_10,
       pc_1_out_11, pc_1_out_12, pc_1_out_13, pc_1_out_14, pc_1_out_15, pc_1_out_16, pc_1_out_17,
       pc_1_out_18, pc_1_out_19, pc_1_out_20, pc_1_out_21, pc_1_out_22, pc_1_out_23, pc_1_out_24,
       pc_1_out_25, PC_INC, ra_1_out_8, ra_1_out_9, ra_1_out_10, ra_1_out_11, ra_1_out_12, ra_1_out_13,
       ra_1_out_14, ra_1_out_15, ra_1_out_18, ra_1_out_19, ra_1_out_20, ra_1_out_21, ra_1_out_22,
       ra_1_out_23, ra_1_out_24, ra_1_out_25, RA_LHS_WRITE, RA_LOAD_DIR, RA_RHS_WRITE, sp_1_out_9,
       sp_1_out_10, sp_1_out_11, sp_1_out_12, sp_1_out_13, sp_1_out_14, sp_1_out_15, sp_1_out_16,
       sp_1_out_17, sp_1_out_18, sp_1_out_19, sp_1_out_20, sp_1_out_21, sp_1_out_22, sp_1_out_23,
       sp_1_out_24, SP_DEC, SP_INC, tcu_1_out_5, tcu_1_out_6, tcu_1_out_7;
  wire [2:0] tcu_1_out_4;
  wire [4:0] ALU_OPS, FLAGS;
  wire [7:0] DATA, gpr_card_1_lhs, ir_1_out, LHS, MEM, RHS, undriven;
  wire [15:0] ADDR, pc_1_ra;
  wire [31:0] decoder_1_p4;

  Clock clock_1 (.out(CLK));
  DotMatrix #(.inputtype("row"), .matrixcols(1), .matrixrows(8)) dotmatrix_1 (
    .row0(DATA[7]), .row1(DATA[6]), .row2(DATA[5]), .row3(DATA[4]), .row4(DATA[3]), .row5(DATA[2]),
    .row6(DATA[1]), .row7(DATA[0]));
  MemBridge membridge_1 (
    .MEMOUT(MEM), .DATAOUT(DATA), .out_5(membridge_1_out_5), .out_6(membridge_1_out_6), .MEM(undriven),
    .DATA(DATA), .in_2(_MEMBRIDGE_DATA_WRITE), .in_3(_MEMBRIDGE_MEM_WRITE));
  DotMatrix #(.inputtype("row"), .matrixcols(1), .matrixrows(8)) dotmatrix_2 (
    .row0(MEM[7]), .row1(MEM[6]), .row2(MEM[5]), .row3(MEM[4]), .row4(MEM[3]), .row5(MEM[2]), .row6(MEM[1]),
    .row7(MEM[0]));
  DotMatrix #(.inputtype("row"), .matrixcols(1), .matrixrows(1)) dotmatrix_3 (.row0(membridge_1_out_6));
  DotMatrix #(.inputtype("row"), .matrixcols(1), .matrixrows(1)) dotmatrix_4 (.row0(membridge_1_out_5));
  TCU tcu_1 (
    .out_5(tcu_1_out_5), .out_6(tcu_1_out_6), .out_7(tcu_1_out_7), .out_4(tcu_1_out_4), ._RESET(in_1),
    .CLK(CLK), ._END_uINSTR(_TCU_RESET));
  DotMatrix #(.matrixcols(8), .matrixrows(1)) dotmatrix_5 (
    .col0(ir_1_out_11), .col1(ir_1_out_10), .col2(ir_1_out_9), .col3(ir_1_out_7), .col4(ir_1_out_6),
    .col5(ir_1_out_5), .col6(ir_1_out_4), .col7(ir_1_out_3));
  IR ir_1 (
    .out_3(ir_1_out_3), .out_4(ir_1_out_4), .out_5(ir_1_out_5), .out_6(ir_1_out_6), .out_7(ir_1_out_7),
    .out_9(ir_1_out_9), .out_10(ir_1_out_10), .out_11(ir_1_out_11), .OUT(ir_1_out), .LOAD(IR_MEM_READ),
    .MEM(MEM));
  DotMatrix #(.matrixcols(1), .matrixrows(1)) dotmatrix_6 (.col0(gpr_card_1_out_5));
  DotMatrix #(.matrixcols(1), .matrixrows(1)) dotmatrix_7 (.col0(gpr_card_1_out_7));
  GPR_Card gpr_card_1 (
    .out_12(gpr_card_1_out_12), .out_13(gpr_card_1_out_13), .out_14(gpr_card_1_out_14),
    .out_15(gpr_card_1_out_15), .out_16(gpr_card_1_out_16), .out_17(gpr_card_1_out_17),
    .out_10(gpr_card_1_out_10), .out_11(gpr_card_1_out_11), .LHS(gpr_card_1_lhs), .RHS(RHS),
    .out_7(gpr_card_1_out_7), .out_6(gpr_card_1_out_6), .out_5(gpr_card_1_out_5), .DATA(DATA),
    .Data_Read(A_DATA_READ), ._RHS_Write(_A_RHS_WRITE), ._LHS_Write(_A_LHS_WRITE));
  DotMatrix #(.matrixcols(1), .matrixrows(1)) dotmatrix_8 (.col0(gpr_card_2_out_5));
  DotMatrix #(.matrixcols(1), .matrixrows(1)) dotmatrix_9 (.col0(gpr_card_2_out_7));
  GPR_Card gpr_card_2 (
    .out_12(gpr_card_2_out_12), .out_13(gpr_card_2_out_13), .out_14(gpr_card_2_out_14),
    .out_15(gpr_card_2_out_15), .out_16(gpr_card_2_out_16), .out_17(gpr_card_2_out_17),
    .out_10(gpr_card_2_out_10), .out_11(gpr_card_2_out_11), .LHS(gpr_card_1_lhs), .RHS(RHS),
    .out_7(gpr_card_2_out_7), .out_6(gpr_card_2_out_6), .out_5(gpr_card_2_out_5), .DATA(DATA),
    .Data_Read(B_DATA_READ), ._RHS_Write(_B_RHS_WRITE), ._LHS_Write(_B_LHS_WRITE));
  DotMatrix #(.matrixcols(1), .matrixrows(1)) dotmatrix_10 (.col0(gpr_card_3_out_5));
  DotMatrix #(.matrixcols(1), .matrixrows(1)) dotmatrix_11 (.col0(gpr_card_3_out_7));
  GPR_Card gpr_card_3 (
    .out_12(gpr_card_3_out_12), .out_13(gpr_card_3_out_13), .out_14(gpr_card_3_out_14),
    .out_15(gpr_card_3_out_15), .out_16(gpr_card_3_out_16), .out_17(gpr_card_3_out_17),
    .out_10(gpr_card_3_out_10), .out_11(gpr_card_3_out_11), .LHS(gpr_card_1_lhs), .RHS(RHS),
    .out_7(gpr_card_3_out_7), .out_6(gpr_card_3_out_6), .out_5(gpr_card_3_out_5), .DATA(DATA),
    .Data_Read(C_DATA_READ), ._RHS_Write(_C_RHS_WRITE), ._LHS_Write(_C_LHS_WRITE));
  DotMatrix #(.matrixcols(4), .matrixrows(1)) dotmatrix_12 (
    .col1(tcu_1_out_7), .col2(tcu_1_out_6), .col3(tcu_1_out_5));  // open: col0
  DotMatrix #(.matrixcols(8), .matrixrows(1)) dotmatrix_13 (
    .col0(ar_card_1_out_13), .col1(ar_card_1_out_15), .col2(ar_card_1_out_17), .col3(ar_card_1_out_19),
    .col4(ar_card_1_out_21), .col5(ar_card_1_out_23), .col6(ar_card_1_out_25), .col7(ar_card_1_out_27));
  AR_CARD ar_card_1 (
    .LHS(gpr_card_1_lhs), .out_13(ar_card_1_out_13), .out_15(ar_card_1_out_15), .out_17(ar_card_1_out_17),
    .out_19(ar_card_1_out_19), .out_21(ar_card_1_out_21), .out_23(ar_card_1_out_23),
    .out_25(ar_card_1_out_25), .out_27(ar_card_1_out_27), .ADDR(ADDR), .out_7(ar_card_1_out_7),
    .out_8(ar_card_1_out_8), .out_9(ar_card_1_out_9), .out_14(ar_card_1_out_14), .out_16(ar_card_1_out_16),
    .out_18(ar_card_1_out_18), .out_20(ar_card_1_out_20), .out_22(ar_card_1_out_22),
    .out_24(ar_card_1_out_24), .out_26(ar_card_1_out_26), .out_28(ar_card_1_out_28), .RHS(RHS),
    .in_2(AR_MEM_READ_lo), .in_3(AR_MEM_READ_hi), .in_4(_ARlo_LHS_WRITE), .in_5(_ARhi_RHS_WRITE),
    .in_6(_AR_ADDR_WRITE), .MEM(undriven));
  DotMatrix #(.matrixcols(1), .matrixrows(1)) dotmatrix_14 (.col0(gpr_card_1_out_6));
  DotMatrix #(.matrixcols(8), .matrixrows(1)) dotmatrix_15 (
    .col0(gpr_card_1_out_10), .col1(gpr_card_1_out_11), .col2(gpr_card_1_out_12), .col3(gpr_card_1_out_13),
    .col4(gpr_card_1_out_14), .col5(gpr_card_1_out_15), .col6(gpr_card_1_out_16), .col7(gpr_card_1_out_17));
  DotMatrix #(.matrixcols(1), .matrixrows(1)) dotmatrix_16 (.col0(gpr_card_2_out_6));
  DotMatrix #(.matrixcols(8), .matrixrows(1)) dotmatrix_17 (
    .col0(gpr_card_2_out_10), .col1(gpr_card_2_out_11), .col2(gpr_card_2_out_12), .col3(gpr_card_2_out_13),
    .col4(gpr_card_2_out_14), .col5(gpr_card_2_out_15), .col6(gpr_card_2_out_16), .col7(gpr_card_2_out_17));
  DotMatrix #(.matrixcols(1), .matrixrows(1)) dotmatrix_18 (.col0(gpr_card_3_out_6));
  DotMatrix #(.matrixcols(8), .matrixrows(1)) dotmatrix_19 (
    .col0(gpr_card_3_out_10), .col1(gpr_card_3_out_11), .col2(gpr_card_3_out_12), .col3(gpr_card_3_out_13),
    .col4(gpr_card_3_out_14), .col5(gpr_card_3_out_15), .col6(gpr_card_3_out_16), .col7(gpr_card_3_out_17));
  // DECODER decoder_1: pin names not known; wires that end beside it: FLAGS, tcu_1_out_4, ir_1_out, decoder_1_p4
  DotMatrix #(.matrixcols(8), .matrixrows(1)) dotmatrix_20 (
    .col0(LHS[7]), .col1(LHS[6]), .col2(LHS[5]), .col3(LHS[4]), .col4(LHS[3]), .col5(LHS[2]), .col6(LHS[1]),
    .col7(LHS[0]));
  DotMatrix #(.matrixcols(8), .matrixrows(1)) dotmatrix_21 (
    .col0(ar_card_1_out_14), .col1(ar_card_1_out_16), .col2(ar_card_1_out_18), .col3(ar_card_1_out_20),
    .col4(ar_card_1_out_22), .col5(ar_card_1_out_24), .col6(ar_card_1_out_26), .col7(ar_card_1_out_28));
  DotMatrix #(.matrixrows(1)) dotmatrix_22 (
    .col0(alu_card_1_out_7), .col1(alu_card_1_out_10), .col2(alu_card_1_out_13), .col3(alu_card_1_out_16),
    .col4(alu_card_1_out_19));
  ALU_CARD alu_card_1 (
    .RESULT(DATA), .FLAGS(FLAGS), .out_7(alu_card_1_out_7), .out_10(alu_card_1_out_10),
    .out_13(alu_card_1_out_13), .out_16(alu_card_1_out_16), .out_19(alu_card_1_out_19),
    .out_8(alu_card_1_out_8), .out_11(alu_card_1_out_11), .out_14(alu_card_1_out_14),
    .out_17(alu_card_1_out_17), .out_20(alu_card_1_out_20), .out_21(alu_card_1_out_21),
    .out_22(alu_card_1_out_22), .out_23(alu_card_1_out_23), .out_9(alu_card_1_out_9),
    .out_12(alu_card_1_out_12), .out_15(alu_card_1_out_15), .out_18(alu_card_1_out_18), .LHS(gpr_card_1_lhs),
    .RHS(RHS), .ALU_OP(ALU_OPS), ._ALU_RESULT(_ALU_DATA_WRITE));
  DotMatrix #(.matrixcols(8), .matrixrows(1)) dotmatrix_23 (
    .col0(memory_1_out_12), .col1(memory_1_out_11), .col2(memory_1_out_9), .col3(memory_1_out_10),
    .col4(memory_1_out_5), .col5(memory_1_out_6), .col6(memory_1_out_7), .col7(memory_1_out_8));
  Memory memory_1 (
    .out_6(memory_1_out_6), .out_7(memory_1_out_7), .out_8(memory_1_out_8), .out_9(memory_1_out_9),
    .out_10(memory_1_out_10), .out_11(memory_1_out_11), .out_12(memory_1_out_12), .out_5(memory_1_out_5),
    .MEM(MEM), .in_2(_RAM_WRITE), .in_3(_RAM_MEM_WRITE), .MEMIN(MEM), .ADDR(ADDR));
  DotMatrix #(.inputtype("row"), .matrixcols(1), .matrixrows(1)) dotmatrix_24 (.row0(ar_card_1_out_7));
  DotMatrix #(.inputtype("row"), .matrixcols(1), .matrixrows(1)) dotmatrix_25 (.row0(ar_card_1_out_8));
  DotMatrix #(.inputtype("row"), .matrixcols(1), .matrixrows(1)) dotmatrix_26 (.row0(ar_card_1_out_9));
  DotMatrix #(.matrixcols(8), .matrixrows(1)) dotmatrix_27 (
    .col0(alu_card_1_out_8), .col1(alu_card_1_out_11), .col2(alu_card_1_out_14), .col3(alu_card_1_out_17),
    .col4(alu_card_1_out_20), .col5(alu_card_1_out_21), .col6(alu_card_1_out_22), .col7(alu_card_1_out_23));
  DotMatrix #(.matrixcols(8), .matrixrows(1)) dotmatrix_28 (
    .col0(RHS[0]), .col1(RHS[1]), .col2(RHS[2]), .col3(RHS[3]), .col4(RHS[4]), .col5(RHS[5]), .col6(RHS[6]),
    .col7(RHS[7]));
  DotMatrix #(.matrixrows(1)) dotmatrix_29 (
    .col1(alu_card_1_out_12), .col2(alu_card_1_out_18), .col3(alu_card_1_out_15), .col4(alu_card_1_out_9));  // open: col0
  DotMatrix #(.matrixrows(1)) dotmatrix_30 (
    .col0(bus_controller_1_out_20), .col1(bus_controller_1_out_16), .col2(bus_controller_1_out_12),
    .col3(bus_controller_1_out_8), .col4(bus_controller_1_out_4));
  BUS_CONTROLLER bus_controller_1 (
    .IR_MEM_READ(IR_MEM_READ), .AR_MEM_READ_lo(AR_MEM_READ_lo), .AR_MEM_READ_hi(AR_MEM_READ_hi),
    ._RAM_MEM_WRITE(_RAM_MEM_WRITE), ._MB_MEM_WRITE(_MEMBRIDGE_MEM_WRITE), .out_23(bus_controller_1_out_23),
    .out_27(bus_controller_1_out_27), .out_33(bus_controller_1_out_33), .out_43(bus_controller_1_out_43),
    .out_47(bus_controller_1_out_47), .out_28(bus_controller_1_out_28), .out_34(bus_controller_1_out_34),
    .out_38(bus_controller_1_out_38), .out_44(bus_controller_1_out_44), .out_48(bus_controller_1_out_48),
    .RA_LOAD_DIR(RA_LOAD_DIR), ._RAM_WRITE(_RAM_WRITE), .PC_INC(PC_INC), .SP_INC(SP_INC), .SP_DEC(SP_DEC),
    ._TCU_RESET(_TCU_RESET), .out_2(bus_controller_1_out_2), .out_6(bus_controller_1_out_6),
    .out_10(bus_controller_1_out_10), .out_14(bus_controller_1_out_14), .out_18(bus_controller_1_out_18),
    .out_50(bus_controller_1_out_50), .A_DATA_READ(A_DATA_READ), .B_DATA_READ(B_DATA_READ),
    .C_DATA_READ(C_DATA_READ), ._MB_DATA_WRITE(_MEMBRIDGE_DATA_WRITE), ._ALU_DATA_WRITE(_ALU_DATA_WRITE),
    ._A_WRITE_LHS(_A_LHS_WRITE), ._B_WRITE_LHS(_B_LHS_WRITE), ._C_WRITE_LHS(_C_LHS_WRITE),
    ._ARlo_WRITE_LHS(_ARlo_LHS_WRITE), ._RA_WRITE_LHS(RA_LHS_WRITE), ._PC_LRHS_READ(_PC_LRHS_READ),
    ._AR_ADDR_WRITE(_AR_ADDR_WRITE), ._PC_ADDR_WRITE(_PC_ADDR_WRITE), ._SP_ADDR_WRITE(_SP_ADDR_WRITE),
    .out_25(bus_controller_1_out_25), .out_31(bus_controller_1_out_31), .out_37(bus_controller_1_out_37),
    .out_4(bus_controller_1_out_4), .out_8(bus_controller_1_out_8), .out_12(bus_controller_1_out_12),
    .out_16(bus_controller_1_out_16), .out_20(bus_controller_1_out_20), .out_40(bus_controller_1_out_40),
    ._A_WRITE_RHS(_A_RHS_WRITE), ._B_WRITE_RHS(_B_RHS_WRITE), ._C_WRITE_RHS(_C_RHS_WRITE),
    ._ARhi_WRITE_RHS(_ARhi_RHS_WRITE), ._RA_WRITE_RHS(RA_RHS_WRITE), ._SP_LRHS_READ(_SP_LRHS_READ),
    .ALU_OPS(ALU_OPS), .DECODE_IN(decoder_1_p4));
  DotMatrix #(.matrixcols(3), .matrixrows(1)) dotmatrix_31 (
    .col0(bus_controller_1_out_37), .col1(bus_controller_1_out_31), .col2(bus_controller_1_out_25));
  DotMatrix #(.matrixcols(16), .matrixrows(1)) dotmatrix_32 (
    .col0(pc_1_out_25), .col1(pc_1_out_24), .col2(pc_1_out_23), .col3(pc_1_out_22), .col4(pc_1_out_21),
    .col5(pc_1_out_20), .col6(pc_1_out_19), .col7(pc_1_out_18), .col8(pc_1_out_17), .col9(pc_1_out_16),
    .col10(pc_1_out_15), .col11(pc_1_out_14), .col12(pc_1_out_13), .col13(pc_1_out_12), .col14(pc_1_out_11),
    .col15(pc_1_out_10));
  PC pc_1 (
    .RA(pc_1_ra), .ADDR(ADDR), .out_10(pc_1_out_10), .out_11(pc_1_out_11), .out_12(pc_1_out_12),
    .out_13(pc_1_out_13), .out_14(pc_1_out_14), .out_15(pc_1_out_15), .out_16(pc_1_out_16),
    .out_17(pc_1_out_17), .out_18(pc_1_out_18), .out_19(pc_1_out_19), .out_20(pc_1_out_20),
    .out_21(pc_1_out_21), .out_22(pc_1_out_22), .out_23(pc_1_out_23), .out_24(pc_1_out_24),
    .out_25(pc_1_out_25), .RESET(in_1), .PC_INC(PC_INC), ._LRHS_READ(_PC_LRHS_READ), .in_6(gpr_card_1_lhs),
    .in_4(_PC_ADDR_WRITE), .in_5(RA_LOAD_DIR), .in_7(RHS));
  DotMatrix #(.matrixcols(8), .matrixrows(1)) dotmatrix_33 (
    .col0(ra_1_out_25), .col1(ra_1_out_24), .col2(ra_1_out_23), .col3(ra_1_out_22), .col4(ra_1_out_21),
    .col5(ra_1_out_20), .col6(ra_1_out_19), .col7(ra_1_out_18));
  RA ra_1 (
    .out_8(ra_1_out_8), .out_9(ra_1_out_9), .out_10(ra_1_out_10), .out_11(ra_1_out_11), .out_12(ra_1_out_12),
    .out_13(ra_1_out_13), .out_14(ra_1_out_14), .out_15(ra_1_out_15), .out_18(ra_1_out_18),
    .out_19(ra_1_out_19), .out_20(ra_1_out_20), .out_21(ra_1_out_21), .out_22(ra_1_out_22),
    .out_23(ra_1_out_23), .out_24(ra_1_out_24), .out_25(ra_1_out_25), .LHSOUT(gpr_card_1_lhs), .RHSOUT(RHS),
    .PC(pc_1_ra), .LHS(gpr_card_1_lhs), .RHS(RHS), .WRITE_RHS(RA_RHS_WRITE), .WRITE_LHS(RA_LHS_WRITE),
    .CPY(CLK), .LOAD_LR(RA_LOAD_DIR));
  DotMatrix #(.matrixcols(16), .matrixrows(1)) dotmatrix_34 (
    .col0(sp_1_out_24), .col1(sp_1_out_23), .col2(sp_1_out_22), .col3(sp_1_out_21), .col4(sp_1_out_20),
    .col5(sp_1_out_19), .col6(sp_1_out_18), .col7(sp_1_out_17), .col8(sp_1_out_16), .col9(sp_1_out_15),
    .col10(sp_1_out_14), .col11(sp_1_out_13), .col12(sp_1_out_12), .col13(sp_1_out_11), .col14(sp_1_out_10),
    .col15(sp_1_out_9));
  SP sp_1 (
    .ADDR(ADDR), .out_9(sp_1_out_9), .out_10(sp_1_out_10), .out_11(sp_1_out_11), .out_12(sp_1_out_12),
    .out_13(sp_1_out_13), .out_14(sp_1_out_14), .out_15(sp_1_out_15), .out_16(sp_1_out_16),
    .out_17(sp_1_out_17), .out_18(sp_1_out_18), .out_19(sp_1_out_19), .out_20(sp_1_out_20),
    .out_21(sp_1_out_21), .out_22(sp_1_out_22), .out_23(sp_1_out_23), .out_24(sp_1_out_24), .RESET(in_1),
    .SP_DEC(SP_DEC), .SP_INC(SP_INC), ._LRHS_READ(_SP_LRHS_READ), .in_6(gpr_card_1_lhs),
    .in_5(_SP_ADDR_WRITE), .in_7(RHS));
  DotMatrix #(.matrixrows(1)) dotmatrix_35 (
    .col0(bus_controller_1_out_18), .col1(bus_controller_1_out_14), .col2(bus_controller_1_out_10),
    .col3(bus_controller_1_out_6), .col4(bus_controller_1_out_2));
  DotMatrix #(.matrixcols(2), .matrixrows(1)) dotmatrix_36 (
    .col0(bus_controller_1_out_40), .col1(bus_controller_1_out_50));
  DotMatrix #(.matrixcols(8), .matrixrows(1)) dotmatrix_37 (
    .col0(ra_1_out_15), .col1(ra_1_out_14), .col2(ra_1_out_13), .col3(ra_1_out_12), .col4(ra_1_out_11),
    .col5(ra_1_out_10), .col6(ra_1_out_9), .col7(ra_1_out_8));
  DotMatrix #(.matrixcols(2), .matrixrows(1)) dotmatrix_38 (
    .col0(bus_controller_1_out_48), .col1(bus_controller_1_out_44));
  DotMatrix #(.matrixcols(2), .matrixrows(1)) dotmatrix_39 (
    .col0(bus_controller_1_out_47), .col1(bus_controller_1_out_43));
  DotMatrix #(.matrixcols(3), .matrixrows(1)) dotmatrix_40 (
    .col0(bus_controller_1_out_38), .col1(bus_controller_1_out_34), .col2(bus_controller_1_out_28));
  DotMatrix #(.matrixcols(3), .matrixrows(1)) dotmatrix_41 (
    .col0(bus_controller_1_out_33), .col1(bus_controller_1_out_27), .col2(bus_controller_1_out_23));
  DotMatrix #(.inputtype("row"), .matrixcols(1), .matrixrows(16)) dotmatrix_42 (
    .row0(ADDR[15]), .row1(ADDR[14]), .row2(ADDR[13]), .row3(ADDR[12]), .row4(ADDR[11]), .row5(ADDR[10]),
    .row6(ADDR[9]), .row7(ADDR[8]), .row8(ADDR[7]), .row9(ADDR[6]), .row10(ADDR[5]), .row11(ADDR[4]),
    .row12(ADDR[3]), .row13(ADDR[2]), .row14(ADDR[1]), .row15(ADDR[0]));

  // Other names for the same wires on the sheet: _RESET = in_1

  // Notes on the sheet:
  //   A
  //   B
  //   C
endmodule

module GPR_Card (
  input  [7:0] DATA,
  input  Data_Read,
  input  _RHS_Write,
  input  _LHS_Write,
  output out_5,
  output out_6,
  output out_7,
  output [7:0] LHS,
  output [7:0] RHS,
  output out_10,
  output out_11,
  output out_12,
  output out_13,
  output out_14,
  output out_15,
  output out_16,
  output out_17
);

  not not_1 (out_7, _LHS_Write);
  not not_2 (out_6, _RHS_Write);
  _74541 u_74541_1 (
    .Q0(LHS[0]), .Q1(LHS[1]), .Q2(LHS[2]), .Q3(LHS[3]), .Q4(LHS[4]), .Q5(LHS[5]), .Q6(LHS[6]), .Q7(LHS[7]),
    ._E0(_LHS_Write), ._E1(1'b0), .D0(out_17), .D1(out_16), .D2(out_15), .D3(out_14), .D4(out_13),
    .D5(out_12), .D6(out_11), .D7(out_10), .GND(1'b0), .VCC(1'b1));
  _74574 u_74574_1 (
    .Q0(out_17), .Q1(out_16), .Q2(out_15), .Q3(out_14), .Q4(out_13), .Q5(out_12), .Q6(out_11), .Q7(out_10),
    .VCC(1'b1), ._OE(1'b0), .CP(Data_Read), .D0(DATA[0]), .D1(DATA[1]), .D2(DATA[2]), .D3(DATA[3]),
    .D4(DATA[4]), .D5(DATA[5]), .D6(DATA[6]), .D7(DATA[7]), .GND(1'b0));
  _74541 u_74541_2 (
    .Q0(RHS[0]), .Q1(RHS[1]), .Q2(RHS[2]), .Q3(RHS[3]), .Q4(RHS[4]), .Q5(RHS[5]), .Q6(RHS[6]), .Q7(RHS[7]),
    ._E0(_RHS_Write), ._E1(1'b0), .D0(out_17), .D1(out_16), .D2(out_15), .D3(out_14), .D4(out_13),
    .D5(out_12), .D6(out_11), .D7(out_10), .GND(1'b0), .VCC(1'b1));

  assign out_5 = Data_Read;

  // Other names for the same wires on the sheet: D0 = DATA[0]; D1 = DATA[1]; D2 = DATA[2]; D3 = DATA[3]; D4 = DATA[4];
  //   D5 = DATA[5]; D6 = DATA[6]; D7 = DATA[7]; L0 = LHS[0]; L1 = LHS[1]; L2 = LHS[2]; L3 = LHS[3]; L4 = LHS[4];
  //   L5 = LHS[5]; L6 = LHS[6]; L7 = LHS[7]; Q0 = out_17; Q1 = out_16; Q2 = out_15; Q3 = out_14; Q4 = out_13;
  //   Q5 = out_12; Q6 = out_11; Q7 = out_10; R0 = RHS[0]; R1 = RHS[1]; R2 = RHS[2]; R3 = RHS[3]; R4 = RHS[4];
  //   R5 = RHS[5]; R6 = RHS[6]; R7 = RHS[7]

  // Notes on the sheet:
  //   BUS INPUTS
  //   BUS OUTPUTS
  //   LED OUTPUTS
  //   MAIN CIRCUIT
endmodule

module ALU_CARD (
  input  [7:0] LHS,
  input  _ALU_RESULT,
  input  [7:0] RHS,
  input  [4:0] ALU_OP,
  output [7:0] RESULT,
  output [4:0] FLAGS,
  output out_7,
  output out_8,
  output out_9,
  output out_10,
  output out_11,
  output out_12,
  output out_13,
  output out_14,
  output out_15,
  output out_16,
  output out_17,
  output out_18,
  output out_19,
  output out_20,
  output out_21,
  output out_22,
  output out_23
);

  wire not_1_out;
  wire [15:0] rom_1_data;
  wire [15:13] ROM_OUT;

  ROM #(.addrWidth(21), .dataWidth(16)) rom_1 (.addr({ALU_OP, RHS, LHS}), .data(rom_1_data));
  not not_1 (not_1_out, _ALU_RESULT);
  assign {ROM_OUT, FLAGS[4:3], FLAGS[1], FLAGS[2], FLAGS[0], out_8, out_11, out_14, out_17, out_20, out_21, out_22, out_23} = not_1_out ? rom_1_data : 16'bz;  // Controlled_Buffer controlled_buffer_1

  assign out_7 = ALU_OP[4];
  assign out_9 = FLAGS[0];
  assign out_10 = ALU_OP[3];
  assign out_12 = FLAGS[1];
  assign out_13 = ALU_OP[2];
  assign out_15 = FLAGS[2];
  assign out_16 = ALU_OP[1];
  assign out_18 = FLAGS[3];
  assign out_19 = ALU_OP[0];

  // Other names for the same wires on the sheet: Out[7:0] = RESULT; L0 = LHS[0]; ROM_ADDR[20:0] = {ALU_OP, RHS, LHS};
  //   L1 = LHS[1]; L2 = LHS[2]; L3 = LHS[3]; L4 = LHS[4]; L5 = LHS[5]; L6 = LHS[6]; L7 = LHS[7]; R0 = RHS[0];
  //   R1 = RHS[1]; R2 = RHS[2]; R3 = RHS[3]; R4 = RHS[4]; R5 = RHS[5]; R6 = RHS[6]; R7 = RHS[7]; Q0 = out_23;
  //   ROM_OUT[12:0] = {FLAGS[4:3], FLAGS[1], FLAGS[2], FLAGS[0], out_8, out_11, out_14, out_17, out_20, out_21, out_22, out_23};
  //   Q1 = out_22; Q2 = out_21; Q3 = out_20; Q4 = out_17; Q5 = out_14; Q6 = out_11; Q7 = out_8; C = FLAGS[0];
  //   V = FLAGS[2]; S = FLAGS[1]; Z = FLAGS[3]; D = FLAGS[4]

  // Notes on the sheet:
  //   BUS INPUTS
  //   BUS OUTPUTS
  //   LED INPUTS
  //   MAIN CIRCUIT
  //   contents of rom_1 (hex, n*v repeats v):
  //   compressed eJztW0t2ozAQ3NcptPaKP81xYjvc/wiROoIRoN9M3vMkebWRBHZVNWqVIvcLYye3wbTTrW1c22nb
  //   aztoO2o7aTs3sO26il6t6+L7N9/fff/w/dP3775fFf9KOavVGKtiJSy/JbfMllY5lVDZlEp5lEQZ
  //   CCeccMIJJ5zw7wrfjhPu4vjH/3k6HNxPh4flcLiYg2PHGBxH+uCY0r5cbtCH3B73uU/BfZ+WxU/V
  //   rBM36iT2OqGEE0444YQTTvh3hX/t8BMBGwdGGWweiGO3mLNY0wpSWNVFFms6QRqrushgTS/IYVUX
  //   SawZBHms6iKBNaOghFVdRLFmkuoER7BmlrrsxpAuaKnJbRzpQpZyZlNIF7KU8ppGupAln9Uc0oUs
  //   uZzmkS5kSWe0hHQhC/1Ov9Pv9Dv9Tr/T77/Q7zQsDUvD/iDDJvNZQrqQ5fPn/37juX/pvgMXTzYr
  //   9agyvUq2ul0UGOCDiDFAawgZBuwxxBiwVSHiDDg+xYUBQR3jwoDIPBwZcKyEhAxIzWTAgEstxTMg
  //   m4uNAbFqjBlQzuZm2GxBqLwiFr9dXTjq1sTbvlldOGpWRVidunCU18WlwnXkKK2MeJUs4MivjUyl
  //   bePIrY5StU45UuuDfqff6Xf6nX6n3+n33+f32vURc7v9hcftgtsFt4sftF1Uv4dg/P/u4R/fQ3D9
  //   4z/I6UzVvnKBg/bfvnLxcrlObvbKtmLCcdfo0I4a08AO+8+h+TNEO/h7pwH2O+147hC7efrsoO0F
  //   cdS+KJ0GNTLRz6ahcerdOLlAbFsYo+Y7HzC6urI=
  //   LED OUTPUTS
endmodule

module MemBridge (
  input  [7:0] MEM,
  input  in_2,
  input  in_3,
  input  [7:0] DATA,
  output out_5,
  output out_6,
  output [7:0] MEMOUT,
  output [7:0] DATAOUT
);

  wire n74541_1_q6;

  _74541 u_74541_1 (
    .Q0(DATAOUT[0]), .Q1(DATAOUT[1]), .Q2(DATAOUT[2]), .Q3(DATAOUT[3]), .Q4(DATAOUT[4]), .Q5(DATAOUT[5]),
    .Q6(n74541_1_q6), .Q7(DATAOUT[7]), ._E0(in_2), ._E1(1'b0), .D0(MEM[0]), .D1(MEM[1]), .D2(MEM[2]),
    .D3(MEM[3]), .D4(MEM[4]), .D5(MEM[5]), .D6(MEM[6]), .D7(MEM[7]), .GND(1'b0), .VCC(1'b1));
  _74541 u_74541_2 (
    .Q0(MEMOUT[0]), .Q1(MEMOUT[1]), .Q2(MEMOUT[2]), .Q3(MEMOUT[3]), .Q4(MEMOUT[4]), .Q5(MEMOUT[5]),
    .Q6(MEMOUT[6]), .Q7(MEMOUT[7]), ._E0(in_3), ._E1(1'b0), .D0(DATA[0]), .D1(DATA[1]), .D2(DATA[2]),
    .D3(DATA[3]), .D4(DATA[4]), .D5(DATA[5]), .D6(DATA[6]), .D7(DATA[7]), .GND(1'b0), .VCC(1'b1));

  assign out_5 = in_2;
  assign out_6 = in_3;

  // Other names for the same wires on the sheet: _DATA_TO_MEM = in_3; _MEM_TO_DATA = in_2; D0 = DATA[0]; D1 = DATA[1];
  //   D2 = DATA[2]; D3 = DATA[3]; D4 = DATA[4]; D5 = DATA[5]; D6 = DATA[6]; D7 = DATA[7]; DATAOUT_0 = DATAOUT[0];
  //   DATAOUT_1 = DATAOUT[1]; DATAOUT_2 = DATAOUT[2]; DATAOUT_3 = DATAOUT[3]; DATAOUT_4 = DATAOUT[4];
  //   DATAOUT_5 = DATAOUT[5]; DATAOUT_6 = DATAOUT[6]; DATAOUT_7 = DATAOUT[7]; M0 = MEM[0]; M1 = MEM[1]; M2 = MEM[2];
  //   M3 = MEM[3]; M4 = MEM[4]; M5 = MEM[5]; M6 = MEM[6]; M7 = MEM[7]; MEMOUT_0 = MEMOUT[0]; MEMOUT_1 = MEMOUT[1];
  //   MEMOUT_2 = MEMOUT[2]; MEMOUT_3 = MEMOUT[3]; MEMOUT_4 = MEMOUT[4]; MEMOUT_5 = MEMOUT[5]; MEMOUT_6 = MEMOUT[6];
  //   MEMOUT_7 = MEMOUT[7]

  // Notes on the sheet:
  //   BUS INPUTS
  //   BUS OUTPUTS
  //   MAIN CIRCUIT
endmodule

module AR_CARD (
  input  [7:0] MEM,
  input  in_2,
  input  in_3,
  input  in_4,
  input  in_5,
  input  in_6,
  output out_7,
  output out_8,
  output out_9,
  output [7:0] LHS,
  output [7:0] RHS,
  output [15:0] ADDR,
  output out_13,
  output out_14,
  output out_15,
  output out_16,
  output out_17,
  output out_18,
  output out_19,
  output out_20,
  output out_21,
  output out_22,
  output out_23,
  output out_24,
  output out_25,
  output out_26,
  output out_27,
  output out_28
);

  not not_1 (out_7, in_4);
  not not_2 (out_8, in_5);
  not not_3 (out_9, in_6);
  _74574 ARlo (
    .Q0(out_27), .Q1(out_25), .Q2(out_23), .Q3(out_21), .Q4(out_19), .Q5(out_17), .Q6(out_15), .Q7(out_13),
    .VCC(1'b1), ._OE(1'b0), .CP(in_2), .D0(MEM[0]), .D1(MEM[1]), .D2(MEM[2]), .D3(MEM[3]), .D4(MEM[4]),
    .D5(MEM[5]), .D6(MEM[6]), .D7(MEM[7]), .GND(1'b0));
  _74541 u_74541_1 (
    .Q0(LHS[0]), .Q1(LHS[1]), .Q2(LHS[2]), .Q3(LHS[3]), .Q4(LHS[4]), .Q5(LHS[5]), .Q6(LHS[6]), .Q7(LHS[7]),
    ._E0(in_4), ._E1(1'b0), .D0(out_27), .D1(out_25), .D2(out_23), .D3(out_21), .D4(out_19), .D5(out_17),
    .D6(out_15), .D7(out_13), .GND(1'b0), .VCC(1'b1));
  _74541 u_74541_2 (
    .Q0(ADDR[0]), .Q1(ADDR[1]), .Q2(ADDR[2]), .Q3(ADDR[3]), .Q4(ADDR[4]), .Q5(ADDR[5]), .Q6(ADDR[6]),
    .Q7(ADDR[7]), ._E0(in_6), ._E1(1'b0), .D0(out_27), .D1(out_25), .D2(out_23), .D3(out_21), .D4(out_19),
    .D5(out_17), .D6(out_15), .D7(out_13), .GND(1'b0), .VCC(1'b1));
  _74574 ARlo_2 (
    .Q0(out_28), .Q1(out_26), .Q2(out_24), .Q3(out_22), .Q4(out_20), .Q5(out_18), .Q6(out_16), .Q7(out_14),
    .VCC(1'b1), ._OE(1'b0), .CP(in_3), .D0(MEM[0]), .D1(MEM[1]), .D2(MEM[2]), .D3(MEM[3]), .D4(MEM[4]),
    .D5(MEM[5]), .D6(MEM[6]), .D7(MEM[7]), .GND(1'b0));
  _74541 u_74541_3 (
    .Q0(RHS[0]), .Q1(RHS[1]), .Q2(RHS[2]), .Q3(RHS[3]), .Q4(RHS[4]), .Q5(RHS[5]), .Q6(RHS[6]), .Q7(RHS[7]),
    ._E0(in_5), ._E1(1'b0), .D0(out_28), .D1(out_26), .D2(out_24), .D3(out_22), .D4(out_20), .D5(out_18),
    .D6(out_16), .D7(out_14), .GND(1'b0), .VCC(1'b1));
  _74541 u_74541_4 (
    .Q0(ADDR[8]), .Q1(ADDR[9]), .Q2(ADDR[10]), .Q3(ADDR[11]), .Q4(ADDR[12]), .Q5(ADDR[13]), .Q6(ADDR[14]),
    .Q7(ADDR[15]), ._E0(in_6), ._E1(1'b0), .D0(out_28), .D1(out_26), .D2(out_24), .D3(out_22), .D4(out_20),
    .D5(out_18), .D6(out_16), .D7(out_14), .GND(1'b0), .VCC(1'b1));

  // Other names for the same wires on the sheet: _ADDR_Write = in_6; _LHS_Write = in_4; _RHS_Write = in_5;
  //   A0 = ADDR[0]; A1 = ADDR[1]; A2 = ADDR[2]; A3 = ADDR[3]; A4 = ADDR[4]; A5 = ADDR[5]; A6 = ADDR[6]; A7 = ADDR[7];
  //   A8 = ADDR[8]; A9 = ADDR[9]; A10 = ADDR[10]; A11 = ADDR[11]; A12 = ADDR[12]; A13 = ADDR[13]; A14 = ADDR[14];
  //   A15 = ADDR[15]; L0 = LHS[0]; L1 = LHS[1]; L2 = LHS[2]; L3 = LHS[3]; L4 = LHS[4]; L5 = LHS[5]; L6 = LHS[6];
  //   L7 = LHS[7]; M0 = MEM[0]; M1 = MEM[1]; M2 = MEM[2]; M3 = MEM[3]; M4 = MEM[4]; M5 = MEM[5]; M6 = MEM[6];
  //   M7 = MEM[7]; MEM_Read_hi = in_3; MEM_Read_lo = in_2; Q0 = out_27; Q1 = out_25; Q2 = out_23; Q3 = out_21;
  //   Q4 = out_19; Q5 = out_17; Q6 = out_15; Q7 = out_13; Q8 = out_28; Q9 = out_26; Q10 = out_24; Q11 = out_22;
  //   Q12 = out_20; Q13 = out_18; Q14 = out_16; Q15 = out_14; R0 = RHS[0]; R1 = RHS[1]; R2 = RHS[2]; R3 = RHS[3];
  //   R4 = RHS[4]; R5 = RHS[5]; R6 = RHS[6]; R7 = RHS[7]

  // Notes on the sheet:
  //   BUS INPUTS
  //   BUS OUTPUTS
  //   LED OUTPUTS
  //   MAIN CIRCUIT
endmodule

module SP (
  input  RESET,
  input  SP_DEC,
  input  SP_INC,
  input  _LRHS_READ,
  input  in_5,
  input  [7:0] in_6,
  input  [7:0] in_7,
  output [15:0] ADDR,
  output out_9,
  output out_10,
  output out_11,
  output out_12,
  output out_13,
  output out_14,
  output out_15,
  output out_16,
  output out_17,
  output out_18,
  output out_19,
  output out_20,
  output out_21,
  output out_22,
  output out_23,
  output out_24
);

  wire n74193_1__bo, n74193_1__co, n74193_2__bo, n74193_2__co, n74193_3__bo, n74193_3__co, Q0, Q1, Q2, Q3,
       Q4, Q5, Q6, Q7, Q8, Q9, Q10, Q11, Q12, Q13, Q14, Q15;

  _74193 u_74193_1 (
    .Q3(Q3), ._CO(n74193_1__co), ._BO(n74193_1__bo), .Q0(Q0), .Q1(Q1), .Q2(Q2), .D3(in_6[3]), .VCC(1'b1),
    .CLR(RESET), ._LD(_LRHS_READ), .UP(SP_INC), .DN(SP_DEC), .GND(1'b0), .D0(in_6[0]), .D1(in_6[1]),
    .D2(in_6[2]));
  _74193 u_74193_2 (
    .Q3(Q7), ._CO(n74193_2__co), ._BO(n74193_2__bo), .Q0(Q4), .Q1(Q5), .Q2(Q6), .D3(in_6[7]), .VCC(1'b1),
    .CLR(RESET), ._LD(_LRHS_READ), .UP(n74193_1__co), .DN(n74193_1__bo), .GND(1'b0), .D0(in_6[4]),
    .D1(in_6[5]), .D2(in_6[6]));
  _74193 u_74193_3 (
    .Q3(Q11), ._CO(n74193_3__co), ._BO(n74193_3__bo), .Q0(Q8), .Q1(Q9), .Q2(Q10), .D3(in_7[3]), .VCC(1'b1),
    .CLR(RESET), ._LD(_LRHS_READ), .UP(n74193_2__co), .DN(n74193_2__bo), .GND(1'b0), .D0(in_7[0]),
    .D1(in_7[1]), .D2(in_7[2]));
  _74193 u_74193_4 (
    .Q3(Q15), .Q0(Q12), .Q1(Q13), .Q2(Q14), .D3(in_7[7]), .VCC(1'b1), .CLR(RESET), ._LD(_LRHS_READ),
    .UP(n74193_3__co), .DN(n74193_3__bo), .GND(1'b0), .D0(in_7[4]), .D1(in_7[5]), .D2(in_7[6]));  // open: _CO, _BO
  _74541 u_74541_1 (
    .Q0(ADDR[0]), .Q1(ADDR[1]), .Q2(ADDR[2]), .Q3(ADDR[3]), .Q4(ADDR[4]), .Q5(ADDR[5]), .Q6(ADDR[6]),
    .Q7(ADDR[7]), ._E0(in_5), ._E1(1'b0), .D0(Q0), .D1(Q1), .D2(Q2), .D3(Q3), .D4(Q4), .D5(Q5), .D6(Q6),
    .D7(Q7), .GND(1'b0), .VCC(1'b1));
  _74541 u_74541_2 (
    .Q0(ADDR[8]), .Q1(ADDR[9]), .Q2(ADDR[10]), .Q3(ADDR[11]), .Q4(ADDR[12]), .Q5(ADDR[13]), .Q6(ADDR[14]),
    .Q7(ADDR[15]), ._E0(in_5), ._E1(1'b0), .D0(Q8), .D1(Q9), .D2(Q10), .D3(Q11), .D4(Q12), .D5(Q13),
    .D6(Q14), .D7(Q15), .GND(1'b0), .VCC(1'b1));

  assign out_9 = ADDR[0];
  assign out_10 = ADDR[1];
  assign out_11 = ADDR[2];
  assign out_12 = ADDR[3];
  assign out_13 = ADDR[4];
  assign out_14 = ADDR[5];
  assign out_15 = ADDR[6];
  assign out_16 = ADDR[7];
  assign out_17 = ADDR[8];
  assign out_18 = ADDR[9];
  assign out_19 = ADDR[10];
  assign out_20 = ADDR[11];
  assign out_21 = ADDR[12];
  assign out_22 = ADDR[13];
  assign out_23 = ADDR[14];
  assign out_24 = ADDR[15];

  // Other names for the same wires on the sheet: _ADDR_WRITE = in_5; A0 = ADDR[0]; A1 = ADDR[1]; A2 = ADDR[2];
  //   A3 = ADDR[3]; A4 = ADDR[4]; A5 = ADDR[5]; A6 = ADDR[6]; A7 = ADDR[7]; A8 = ADDR[8]; A9 = ADDR[9];
  //   A10 = ADDR[10]; A11 = ADDR[11]; A12 = ADDR[12]; A13 = ADDR[13]; A14 = ADDR[14]; A15 = ADDR[15]; L0 = in_6[0];
  //   L1 = in_6[1]; L2 = in_6[2]; L3 = in_6[3]; L4 = in_6[4]; L5 = in_6[5]; L6 = in_6[6]; L7 = in_6[7]; R0 = in_7[0];
  //   R1 = in_7[1]; R2 = in_7[2]; R3 = in_7[3]; R4 = in_7[4]; R5 = in_7[5]; R6 = in_7[6]; R7 = in_7[7]
endmodule

module PC (
  input  RESET,
  input  PC_INC,
  input  _LRHS_READ,
  input  in_4,
  input  in_5,
  input  [7:0] in_6,
  input  [7:0] in_7,
  output [15:0] ADDR,
  output [15:0] RA,
  output out_10,
  output out_11,
  output out_12,
  output out_13,
  output out_14,
  output out_15,
  output out_16,
  output out_17,
  output out_18,
  output out_19,
  output out_20,
  output out_21,
  output out_22,
  output out_23,
  output out_24,
  output out_25
);

  wire n74193_1__bo, n74193_1__co, n74193_2__bo, n74193_2__co, n74193_3__bo, n74193_3__co, Q0, Q1, Q2, Q3,
       Q4, Q5, Q6, Q7, Q8, Q9, Q10, Q11, Q12, Q13, Q14, Q15;

  _74193 u_74193_1 (
    .Q3(Q3), ._CO(n74193_1__co), ._BO(n74193_1__bo), .Q0(Q0), .Q1(Q1), .Q2(Q2), .D3(in_6[3]), .VCC(1'b1),
    .CLR(RESET), ._LD(_LRHS_READ), .UP(PC_INC), .DN(1'b1), .GND(1'b0), .D0(in_6[0]), .D1(in_6[1]),
    .D2(in_6[2]));
  _74193 u_74193_2 (
    .Q3(Q7), ._CO(n74193_2__co), ._BO(n74193_2__bo), .Q0(Q4), .Q1(Q5), .Q2(Q6), .D3(in_6[7]), .VCC(1'b1),
    .CLR(RESET), ._LD(_LRHS_READ), .UP(n74193_1__co), .DN(n74193_1__bo), .GND(1'b0), .D0(in_6[4]),
    .D1(in_6[5]), .D2(in_6[6]));
  _74193 u_74193_3 (
    .Q3(Q11), ._CO(n74193_3__co), ._BO(n74193_3__bo), .Q0(Q8), .Q1(Q9), .Q2(Q10), .D3(in_7[3]), .VCC(1'b1),
    .CLR(RESET), ._LD(_LRHS_READ), .UP(n74193_2__co), .DN(n74193_2__bo), .GND(1'b0), .D0(in_7[0]),
    .D1(in_7[1]), .D2(in_7[2]));
  _74193 u_74193_4 (
    .Q3(Q15), .Q0(Q12), .Q1(Q13), .Q2(Q14), .D3(in_7[7]), .VCC(1'b1), .CLR(RESET), ._LD(_LRHS_READ),
    .UP(n74193_3__co), .DN(n74193_3__bo), .GND(1'b0), .D0(in_7[4]), .D1(in_7[5]), .D2(in_7[6]));  // open: _CO, _BO
  _74541 u_74541_1 (
    .Q0(ADDR[0]), .Q1(ADDR[1]), .Q2(ADDR[2]), .Q3(ADDR[3]), .Q4(ADDR[4]), .Q5(ADDR[5]), .Q6(ADDR[6]),
    .Q7(ADDR[7]), ._E0(in_4), ._E1(1'b0), .D0(Q0), .D1(Q1), .D2(Q2), .D3(Q3), .D4(Q4), .D5(Q5), .D6(Q6),
    .D7(Q7), .GND(1'b0), .VCC(1'b1));
  _74541 u_74541_2 (
    .Q0(ADDR[8]), .Q1(ADDR[9]), .Q2(ADDR[10]), .Q3(ADDR[11]), .Q4(ADDR[12]), .Q5(ADDR[13]), .Q6(ADDR[14]),
    .Q7(ADDR[15]), ._E0(in_4), ._E1(1'b0), .D0(Q8), .D1(Q9), .D2(Q10), .D3(Q11), .D4(Q12), .D5(Q13),
    .D6(Q14), .D7(Q15), .GND(1'b0), .VCC(1'b1));
  _74541 u_74541_3 (
    .Q0(RA[0]), .Q1(RA[1]), .Q2(RA[2]), .Q3(RA[3]), .Q4(RA[4]), .Q5(RA[5]), .Q6(RA[6]), .Q7(RA[7]),
    ._E0(in_5), ._E1(1'b0), .D0(Q0), .D1(Q1), .D2(Q2), .D3(Q3), .D4(Q4), .D5(Q5), .D6(Q6), .D7(Q7),
    .GND(1'b0), .VCC(1'b1));
  _74541 u_74541_4 (
    .Q0(RA[8]), .Q1(RA[9]), .Q2(RA[10]), .Q3(RA[11]), .Q4(RA[12]), .Q5(RA[13]), .Q6(RA[14]), .Q7(RA[15]),
    ._E0(in_5), ._E1(1'b0), .D0(Q8), .D1(Q9), .D2(Q10), .D3(Q11), .D4(Q12), .D5(Q13), .D6(Q14), .D7(Q15),
    .GND(1'b0), .VCC(1'b1));

  assign out_10 = ADDR[0];
  assign out_11 = ADDR[1];
  assign out_12 = ADDR[2];
  assign out_13 = ADDR[3];
  assign out_14 = ADDR[4];
  assign out_15 = ADDR[5];
  assign out_16 = ADDR[6];
  assign out_17 = ADDR[7];
  assign out_18 = ADDR[8];
  assign out_19 = ADDR[9];
  assign out_20 = ADDR[10];
  assign out_21 = ADDR[11];
  assign out_22 = ADDR[12];
  assign out_23 = ADDR[13];
  assign out_24 = ADDR[14];
  assign out_25 = ADDR[15];

  // Other names for the same wires on the sheet: _ADDR_WRITE = in_4; _RA_WRITE = in_5; A0 = ADDR[0]; A1 = ADDR[1];
  //   A2 = ADDR[2]; A3 = ADDR[3]; A4 = ADDR[4]; A5 = ADDR[5]; A6 = ADDR[6]; A7 = ADDR[7]; A8 = ADDR[8]; A9 = ADDR[9];
  //   A10 = ADDR[10]; A11 = ADDR[11]; A12 = ADDR[12]; A13 = ADDR[13]; A14 = ADDR[14]; A15 = ADDR[15]; L0 = in_6[0];
  //   L1 = in_6[1]; L2 = in_6[2]; L3 = in_6[3]; L4 = in_6[4]; L5 = in_6[5]; L6 = in_6[6]; L7 = in_6[7]; R0 = in_7[0];
  //   R1 = in_7[1]; R2 = in_7[2]; R3 = in_7[3]; R4 = in_7[4]; R5 = in_7[5]; R6 = in_7[6]; R7 = in_7[7]
endmodule

module RA (
  input  LOAD_LR,
  input  [15:0] PC,
  input  WRITE_LHS,
  input  [7:0] LHS,
  input  CPY,
  input  WRITE_RHS,
  input  [7:0] RHS,
  output out_8,
  output out_9,
  output out_10,
  output out_11,
  output out_12,
  output out_13,
  output out_14,
  output out_15,
  output [7:0] LHSOUT,
  output [7:0] RHSOUT,
  output out_18,
  output out_19,
  output out_20,
  output out_21,
  output out_22,
  output out_23,
  output out_24,
  output out_25
);

  wire n7404_1_y0;
  wire [7:0] n74541_1_q0, n74541_2_q0;

  _7404 u_7404_1 (.Y0(n7404_1_y0), .A0(LOAD_LR));  // open: Y5, Y4, Y3, Y1, Y2, A5, A4, A3, VCC, A1, A2, GND
  _74541 u_74541_1 (
    .Q0(n74541_1_q0[0]), .Q1(n74541_1_q0[1]), .Q2(n74541_1_q0[2]), .Q3(n74541_1_q0[3]), .Q4(n74541_1_q0[4]),
    .Q5(n74541_1_q0[5]), .Q6(n74541_1_q0[6]), .Q7(n74541_1_q0[7]), ._E0(LOAD_LR), ._E1(1'b0), .D0(PC[0]),
    .D1(PC[1]), .D2(PC[2]), .D3(PC[3]), .D4(PC[4]), .D5(PC[5]), .D6(PC[6]), .D7(PC[7]), .GND(1'b0), .VCC(1'b1));
  _74541 u_74541_2 (
    .Q0(n74541_2_q0[0]), .Q1(n74541_2_q0[1]), .Q2(n74541_2_q0[2]), .Q3(n74541_2_q0[3]), .Q4(n74541_2_q0[4]),
    .Q5(n74541_2_q0[5]), .Q6(n74541_2_q0[6]), .Q7(n74541_2_q0[7]), ._E1(1'b0), .D0(PC[8]), .D1(PC[9]),
    .D2(PC[10]), .D3(PC[11]), .D4(PC[12]), .D5(PC[13]), .D6(PC[14]), .D7(PC[15]), .GND(1'b0), .VCC(1'b1));  // open: _E0
  _74541 u_74541_3 (
    .Q0(n74541_1_q0[0]), .Q1(n74541_1_q0[1]), .Q2(n74541_1_q0[2]), .Q3(n74541_1_q0[3]), .Q4(n74541_1_q0[4]),
    .Q5(n74541_1_q0[5]), .Q6(n74541_1_q0[6]), .Q7(n74541_1_q0[7]), ._E0(n7404_1_y0), ._E1(1'b0), .D0(LHS[0]),
    .D1(LHS[1]), .D2(LHS[2]), .D3(LHS[3]), .D4(LHS[4]), .D5(LHS[5]), .D6(LHS[6]), .D7(LHS[7]), .GND(1'b0),
    .VCC(1'b1));
  _74541 u_74541_4 (
    .Q0(n74541_2_q0[0]), .Q1(n74541_2_q0[1]), .Q2(n74541_2_q0[2]), .Q3(n74541_2_q0[3]), .Q4(n74541_2_q0[4]),
    .Q5(n74541_2_q0[5]), .Q6(n74541_2_q0[6]), .Q7(n74541_2_q0[7]), ._E0(n7404_1_y0), ._E1(1'b0), .D0(RHS[0]),
    .D1(RHS[1]), .D2(RHS[2]), .D3(RHS[3]), .D4(RHS[4]), .D5(RHS[5]), .D6(RHS[6]), .D7(RHS[7]), .GND(1'b0),
    .VCC(1'b1));
  _74574 u_74574_1 (
    .Q0(LHSOUT[0]), .Q1(LHSOUT[1]), .Q2(LHSOUT[2]), .Q3(LHSOUT[3]), .Q4(LHSOUT[4]), .Q5(LHSOUT[5]),
    .Q6(LHSOUT[6]), .Q7(LHSOUT[7]), .VCC(1'b1), ._OE(WRITE_LHS), .CP(CPY), .D0(n74541_1_q0[0]),
    .D1(n74541_1_q0[1]), .D2(n74541_1_q0[2]), .D3(n74541_1_q0[3]), .D4(n74541_1_q0[4]), .D5(n74541_1_q0[5]),
    .D6(n74541_1_q0[6]), .D7(n74541_1_q0[7]), .GND(1'b0));
  _74574 u_74574_2 (
    .Q0(out_18), .Q1(out_19), .Q2(out_20), .Q3(out_21), .Q4(out_22), .Q5(out_23), .Q6(out_24), .Q7(out_25),
    .VCC(1'b1), ._OE(WRITE_RHS), .CP(CPY), .D0(n74541_2_q0[0]), .D1(n74541_2_q0[1]), .D2(n74541_2_q0[2]),
    .D3(n74541_2_q0[3]), .D4(n74541_2_q0[4]), .D5(n74541_2_q0[5]), .D6(n74541_2_q0[6]), .D7(n74541_2_q0[7]),
    .GND(1'b0));

  assign out_8 = LHSOUT[0];
  assign out_9 = LHSOUT[1];
  assign out_10 = LHSOUT[2];
  assign out_11 = LHSOUT[3];
  assign out_12 = LHSOUT[4];
  assign out_13 = LHSOUT[5];
  assign out_14 = LHSOUT[6];
  assign out_15 = LHSOUT[7];
  assign RHSOUT = {out_25, out_24, out_23, out_22, out_21, out_20, out_19, out_18};
endmodule

module Memory (
  input  [15:0] ADDR,
  input  in_2,
  input  in_3,
  input  [7:0] MEMIN,
  output out_5,
  output out_6,
  output out_7,
  output out_8,
  output out_9,
  output out_10,
  output out_11,
  output out_12,
  output [7:0] MEM
);

  wire and_1_out, and_2_out, not_1_out, not_2_out, not_3_out, not_4_out;
  wire [7:0] controlled_buffer_2_out, ram_1_data, rom_1_data;

  not not_1 (not_1_out, in_3);
  not not_2 (not_2_out, ADDR[15]);
  not not_3 (not_3_out, in_2);
  ROM #(.addrWidth(15)) rom_1 (.addr(ADDR[14:0]), .data(rom_1_data));
  and and_1 (and_1_out, ADDR[15], in_3);
  and and_2 (and_2_out, not_2_out, in_3);
  RAM #(.addrWidth(15), .databus("bidir"), .trigger("high")) ram_1 (
    .addr(ADDR[14:0]), .data(ram_1_data));  // open: we, oe, clk
  not not_4 (not_4_out, not_3_out);
  assign ram_1_data = not_3_out ? MEMIN : 8'bz;  // Controlled_Buffer controlled_buffer_1
  // Probe on ram_1_data
  assign controlled_buffer_2_out = and_1_out ? rom_1_data : 8'bz;  // Controlled_Buffer controlled_buffer_2
  assign controlled_buffer_2_out = and_2_out ? ram_1_data : 8'bz;  // Controlled_Buffer controlled_buffer_3
  assign MEM = not_1_out ? controlled_buffer_2_out : 8'bz;  // Controlled_Buffer controlled_buffer_4

  assign out_5 = MEM[0];
  assign out_6 = MEM[1];
  assign out_7 = MEM[2];
  assign out_8 = MEM[3];
  assign out_9 = MEM[4];
  assign out_10 = MEM[5];
  assign out_11 = MEM[6];
  assign out_12 = MEM[7];

  // Other names for the same wires on the sheet: _MEM_OUT = in_3; _RAM_WRITE = in_2; ADDR_0_14[14:0] = ADDR[14:0];
  //   ADDR_15 = ADDR[15]; MEM_IN[7:0] = MEMIN
endmodule

module TCU (
  input  _RESET,
  input  CLK,
  input  _END_uINSTR,
  output [2:0] out_4,
  output out_5,
  output out_6,
  output out_7
);

  wire n74163_1_q3;

  _74163 u_74163_1 (
    .Q0(out_4[0]), .Q1(out_4[1]), .Q2(out_4[2]), .Q3(n74163_1_q3), .CP(CLK), .D0(1'b0), .D1(1'b0), .D2(1'b0),
    .D3(1'b0), .ENP(1'b1), .GND(1'b0), ._CLR(_RESET), .ENT(1'b1), ._LD(_END_uINSTR), .VCC(1'b1));  // open: RCO

  assign out_5 = out_4[0];
  assign out_6 = out_4[1];
  assign out_7 = out_4[2];
endmodule

module DECODER (
  input  [7:0] INSTR,
  input  [2:0] uCOUNT,
  input  [4:0] Flags,
  output [31:0] OUT
);

  ROM #(.addrWidth(16), .dataWidth(16)) rom_1 (.data(OUT[15:0]));  // open: addr
  ROM #(.addrWidth(16), .dataWidth(16)) rom_2 (.addr({Flags, uCOUNT, INSTR}), .data(OUT[31:16]));
endmodule

module IR (
  input  [7:0] MEM,
  input  LOAD,
  output out_3,
  output out_4,
  output out_5,
  output out_6,
  output out_7,
  output [7:0] OUT,
  output out_9,
  output out_10,
  output out_11
);

  _74574 u_74574_1 (
    .Q0(OUT[0]), .Q1(OUT[1]), .Q2(OUT[2]), .Q3(OUT[3]), .Q4(OUT[4]), .Q5(OUT[5]), .Q6(OUT[6]), .Q7(OUT[7]),
    .VCC(1'b1), ._OE(1'b0), .CP(LOAD), .D0(MEM[0]), .D1(MEM[1]), .D2(MEM[2]), .D3(MEM[3]), .D4(MEM[4]),
    .D5(MEM[5]), .D6(MEM[6]), .D7(MEM[7]), .GND(1'b0));

  assign out_3 = OUT[0];
  assign out_4 = OUT[1];
  assign out_5 = OUT[2];
  assign out_6 = OUT[3];
  assign out_7 = OUT[4];
  assign out_9 = OUT[5];
  assign out_10 = OUT[6];
  assign out_11 = OUT[7];
endmodule

module BUS_CONTROLLER (
  input  [31:0] DECODE_IN,
  output out_2,
  output _A_WRITE_LHS,
  output out_4,
  output _A_WRITE_RHS,
  output out_6,
  output _B_WRITE_LHS,
  output out_8,
  output _B_WRITE_RHS,
  output out_10,
  output _C_WRITE_LHS,
  output out_12,
  output _C_WRITE_RHS,
  output out_14,
  output _ARlo_WRITE_LHS,
  output out_16,
  output _ARhi_WRITE_RHS,
  output out_18,
  output _RA_WRITE_LHS,
  output out_20,
  output _RA_WRITE_RHS,
  output IR_MEM_READ,
  output out_23,
  output _AR_ADDR_WRITE,
  output out_25,
  output AR_MEM_READ_lo,
  output out_27,
  output out_28,
  output A_DATA_READ,
  output _PC_ADDR_WRITE,
  output out_31,
  output AR_MEM_READ_hi,
  output out_33,
  output out_34,
  output B_DATA_READ,
  output _SP_ADDR_WRITE,
  output out_37,
  output out_38,
  output C_DATA_READ,
  output out_40,
  output _SP_LRHS_READ,
  output _RAM_MEM_WRITE,
  output out_43,
  output out_44,
  output _MB_DATA_WRITE,
  output _MB_MEM_WRITE,
  output out_47,
  output out_48,
  output _ALU_DATA_WRITE,
  output out_50,
  output _PC_LRHS_READ,
  output RA_LOAD_DIR,
  output _RAM_WRITE,
  output PC_INC,
  output SP_INC,
  output [4:0] ALU_OPS,
  output SP_DEC,
  output _TCU_RESET
);

  _74139 MEM___DATA_READ (
    ._11__2Y1(A_DATA_READ), ._10__2Y2(B_DATA_READ), ._9__2Y3(C_DATA_READ), ._5__1Y1(IR_MEM_READ),
    ._6__1Y2(AR_MEM_READ_lo), ._7__1Y3(AR_MEM_READ_hi), ._15__2G(1'b0), ._14__2A(DECODE_IN[14]),
    ._13__2B(DECODE_IN[15]), ._16__Vcc(1'b1), ._2__1A(DECODE_IN[12]), ._3__1B(DECODE_IN[13]), ._8__GND(1'b0),
    ._1__1G(1'b0));  // open: _12__2Y0, _4__1Y0
  _74139 MEM___DATA_WRITE (
    ._11__2Y1(_MB_DATA_WRITE), ._10__2Y2(_ALU_DATA_WRITE), ._6__1Y2(_RAM_MEM_WRITE), ._7__1Y3(_MB_MEM_WRITE),
    ._15__2G(1'b0), ._14__2A(DECODE_IN[2]), ._13__2B(DECODE_IN[3]), ._16__Vcc(1'b1), ._2__1A(DECODE_IN[0]),
    ._3__1B(DECODE_IN[1]), ._8__GND(1'b0), ._1__1G(1'b0));  // open: _12__2Y0, _9__2Y3, _4__1Y0, _5__1Y1
  _74138 LHS_WRITE (
    .Y1(_A_WRITE_LHS), .Y2(_B_WRITE_LHS), .Y3(_C_WRITE_LHS), .Y4(_ARlo_WRITE_LHS), .Y5(_RA_WRITE_LHS),
    .VCC(1'b1), .B(DECODE_IN[5]), .C(DECODE_IN[6]), ._EA(1'b0), ._EB(1'b0), .E(1'b1), .GND(1'b0),
    .A(DECODE_IN[4]));  // open: Y0, Y6, Y7
  _74138 RHS_WRITE (
    .Y1(_A_WRITE_RHS), .Y2(_B_WRITE_RHS), .Y3(_C_WRITE_RHS), .Y4(_ARhi_WRITE_RHS), .Y5(_RA_WRITE_RHS),
    .VCC(1'b1), .B(DECODE_IN[8]), .C(DECODE_IN[9]), ._EA(1'b0), ._EB(1'b0), .E(1'b1), .GND(1'b0),
    .A(DECODE_IN[7]));  // open: Y0, Y6, Y7
  _74139 ADDR_WRITE (
    ._5__1Y1(_AR_ADDR_WRITE), ._6__1Y2(_PC_ADDR_WRITE), ._7__1Y3(_SP_ADDR_WRITE), ._15__2G(1'b0),
    ._16__Vcc(1'b1), ._2__1A(DECODE_IN[10]), ._3__1B(DECODE_IN[11]), ._8__GND(1'b0), ._1__1G(1'b0));  // open: _12__2Y0, _11__2Y1, _10__2Y2, _9__2Y3, _4__1Y0, _14__2A, _13__2B

  assign _PC_LRHS_READ = DECODE_IN[24];
  assign _RAM_WRITE = DECODE_IN[22];
  assign _SP_LRHS_READ = DECODE_IN[16];
  assign _TCU_RESET = DECODE_IN[28];
  assign ALU_OPS = DECODE_IN[21:17];
  assign out_2 = _A_WRITE_LHS;
  assign out_4 = _A_WRITE_RHS;
  assign out_6 = _B_WRITE_LHS;
  assign out_8 = _B_WRITE_RHS;
  assign out_10 = _C_WRITE_LHS;
  assign out_12 = _C_WRITE_RHS;
  assign out_14 = _ARlo_WRITE_LHS;
  assign out_16 = _ARhi_WRITE_RHS;
  assign out_18 = _RA_WRITE_LHS;
  assign out_20 = _RA_WRITE_RHS;
  assign out_23 = IR_MEM_READ;
  assign out_25 = _AR_ADDR_WRITE;
  assign out_27 = AR_MEM_READ_lo;
  assign out_28 = A_DATA_READ;
  assign out_31 = _PC_ADDR_WRITE;
  assign out_33 = AR_MEM_READ_hi;
  assign out_34 = B_DATA_READ;
  assign out_37 = _SP_ADDR_WRITE;
  assign out_38 = C_DATA_READ;
  assign out_40 = DECODE_IN[16];
  assign out_43 = _RAM_MEM_WRITE;
  assign out_44 = _MB_DATA_WRITE;
  assign out_47 = _MB_MEM_WRITE;
  assign out_48 = _ALU_DATA_WRITE;
  assign out_50 = DECODE_IN[24];
  assign PC_INC = DECODE_IN[25];
  assign RA_LOAD_DIR = DECODE_IN[23];
  assign SP_DEC = DECODE_IN[27];
  assign SP_INC = DECODE_IN[26];

  // Other names for the same wires on the sheet: ALUOP_0 = DECODE_IN[17]; ALUOP_1 = DECODE_IN[18];
  //   ALUOP_2 = DECODE_IN[19]; ALUOP_3 = DECODE_IN[20]; ALUOP_4 = DECODE_IN[21]; MEM_WRITE_SEL0 = DECODE_IN[0];
  //   MEM_WRITE_SEL1 = DECODE_IN[1]; DATA_WRITE_SEL0 = DECODE_IN[2]; DATA_WRITE_SEL1 = DECODE_IN[3];
  //   LHS_WRITE_SEL_0 = DECODE_IN[4]; LHS_WRITE_SEL_1 = DECODE_IN[5]; LHS_WRITE_SEL_2 = DECODE_IN[6];
  //   RHS_WRITE_SEL_0 = DECODE_IN[7]; RHS_WRITE_SEL_1 = DECODE_IN[8]; RHS_WRITE_SEL_2 = DECODE_IN[9];
  //   ADDR_WRITE_SEL_0 = DECODE_IN[10]; ADDR_WRITE_SEL_1 = DECODE_IN[11]; MEM_READ_SEL_0 = DECODE_IN[12];
  //   MEM_READ_SEL_1 = DECODE_IN[13]; DATA_READ_SEL_0 = DECODE_IN[14]; DATA_READ_SEL_1 = DECODE_IN[15];
  //   SP_LRHS_READ = DECODE_IN[16]; _PC_LOAD = DECODE_IN[24]

  // Notes on the sheet:
  //   LHS / RHS:
  //   - Device 0 : None
  //   - Device 1 : A
  //   - Device 2 : B
  //   - Device 3 : C
  //   - Device 4 : AR
  //   - Device 5: RA
endmodule
