// Digital circuit cpu.dig as structural Verilog
module cpu (
  input  clk,
  input  in_2
);

  wire a_read_data, a_read_data_reset, a_write_lhs, a_write_rhs, alu_1_p1, alu_1_p7, alu_write_data,
       ax_read_addr, axh_write_lhs, axl_write_rhs, b_read_data, b_read_data_reset, b_write_lhs, b_write_rhs,
       c_read_data, c_read_data_reset, c_write_lhs, c_write_rhs, clk_t, d_read_data, d_read_data_reset,
       d_write_lhs, d_write_rhs, device0_read_data, device0_write_data, device1_read_data,
       device1_write_data, device2_read_data, device2_write_data, device3_read_data, device3_write_data,
       device4_read_data, device4_write_data, device5_read_data, device6_read_data, device7_read_data,
       device8_read_data, device9_read_data, device10_read_data, ir_led_ctrl, ir_read_mem, ir_read_mem_reset,
       mb_write_data, mb_write_data_reset, mb_write_mem, mem_out, mx_write_addr, mxh_read_mem,
       mxh_read_mem_reset, mxh_write_lhs, mxl_read_mem, mxl_read_mem_reset, mxl_write_rhs, not_1_out, pc_dec,
       pc_inc, pc_out, pc_read_lrhs, pc_write_addr, ra_read_lhs, ra_read_pc, ra_read_rhs, ra_write_lhs,
       ra_write_rhs, ram_write, reset, reset_2_out, reset_t, rti, si_dec, si_inc, si_read_lrhs,
       si_write_addr, sp_dec, sp_inc, sp_read_lrhs, sp_write_addr, tcu_end_seq, tcu_led_end;
  wire [1:0] axh_led_ctrl, axl_led_ctrl, mem_bridge_led_ctrl, memory_1_p5;
  wire [2:0] a_led_ctrl, b_led_ctrl, c_led_ctrl, d_led_ctrl, seq;
  wire [3:0] mxh_led_ctrl, mxl_led_ctrl, pc_p12, ra_p9, si_led_ctrl, sp_led_ctrl;
  wire [4:0] alu_op, flags;
  wire [7:0] a_led_val, addr_hi, addr_lo, b_led_val, c_led_val, d_led_val, data, instruction, lhs, mem,
       mxh_led_val, mxl_led_val, rhs;
  wire [15:0] addr, decoder_0_data, decoder_1_data, pc_p13, ra_p11, si_led_count, sp_led_count;

  decoder_0 decoder_0 (.data(decoder_0_data), .flags_in({5{1'b0}}), .ir_in(instruction), .tcu_in(seq));
  decoder_1 decoder_1 (.data(decoder_1_data), .flags_in({5{1'b0}}), .ir_in(instruction), .tcu_in(seq));
  // Probe on decoder_0_data
  // Probe on decoder_1_data
  _7404 _7404_1 (
    .pin1(clk), .pin2(clk_t), .pin3(reset_t), .pin4(reset), .pin5(1'b0), .pin7(1'b0), .pin9(1'b0),
    .pin11(1'b0), .pin13(1'b0), .pin14(1'b1));  // open: pin6, pin8, pin10, pin12
  bus_controller bus_controller (
    .clk(clk_t), .decoder_in0(decoder_0_data), .decoder_in1(decoder_1_data),
    .out({ax_read_addr, ra_read_pc, ra_read_rhs, ra_read_lhs, rti, tcu_end_seq, pc_inc, ram_write, si_dec, sp_dec, si_inc, sp_inc, pc_dec, si_write_addr, sp_write_addr, pc_write_addr, mx_write_addr, si_read_lrhs, sp_read_lrhs, pc_read_lrhs, axl_write_rhs, ra_write_rhs, d_write_rhs, c_write_rhs, b_write_rhs, a_write_rhs, mxl_write_rhs, axh_write_lhs, ra_write_lhs, d_write_lhs, c_write_lhs, b_write_lhs, a_write_lhs, mxh_write_lhs, device10_read_data, device9_read_data, device8_read_data, device7_read_data, device6_read_data, device5_read_data, device4_read_data, device3_read_data, device2_read_data, device1_read_data, device0_read_data, d_read_data, c_read_data, b_read_data, a_read_data, device4_write_data, device3_write_data, device2_write_data, device1_write_data, device0_write_data, alu_write_data, mb_write_data, mxl_read_mem, mxh_read_mem, ir_read_mem, mb_write_mem, mem_out}),
    .alu_op(alu_op));
  // memory memory_1: pin names not known; wires that end beside it: addr, mem_out, ram_write, reset, memory_1_p5, mem, mem[4]
  LED led_1 (.in(memory_1_p5[0]));
  LED led_2 (.in(memory_1_p5[1]));
  // Probe on mem
  LED led_3 (.in(mem[7]));
  LED led_4 (.in(mem[6]));
  LED led_5 (.in(mem[5]));
  LED led_6 (.in(mem[4]));
  LED led_7 (.in(mem[3]));
  LED led_8 (.in(mem[2]));
  LED led_9 (.in(mem[1]));
  LED led_10 (.in(mem[0]));
  reset reset_1 (
    .reset(reset), .mb_write_data(mb_write_data), .mxh_read_mem(mxh_read_mem), .mxl_read_mem(mxl_read_mem),
    .ir_read_mem(ir_read_mem), .a_read_data(a_read_data), .b_read_data(b_read_data),
    .c_read_data(c_read_data), .d_read_data(d_read_data), .mb_write_data_reset(mb_write_data_reset),
    .mxh_read_mem_reset(mxh_read_mem_reset), .mxl_read_mem_reset(mxl_read_mem_reset),
    .ir_read_mem_reset(ir_read_mem_reset), .a_read_data_reset(a_read_data_reset),
    .b_read_data_reset(b_read_data_reset), .c_read_data_reset(c_read_data_reset),
    .d_read_data_reset(d_read_data_reset), .mem(mem));
  LED led_11 (.in(mxh_led_ctrl[0]));
  LED led_12 (.in(mxl_led_ctrl[0]));
  mem_bridge mem_bridge (
    .write_mem(mb_write_mem), .data_in(data), .write_data(mb_write_data_reset), .mem_in(mem),
    .led_ctrl(mem_bridge_led_ctrl), .data_out(data), .mem_out(mem));
  LED led_13 (.in(mxh_led_ctrl[1]));
  LED led_14 (.in(mxh_led_ctrl[2]));
  LED led_15 (.in(mxh_led_ctrl[3]));
  mem_xfer mxh (
    .led_ctrl(mxh_led_ctrl), .lhs(lhs), .addr(addr_hi), .led_val(mxh_led_val), .read_mem(mxh_read_mem_reset),
    .write_lhs(1'b1), .write_rhs(mxh_write_lhs), .write_addr(mx_write_addr), .mem(mem));  // open: rhs
  LED led_16 (.in(mxl_led_ctrl[1]));
  LED led_17 (.in(mxl_led_ctrl[2]));
  LED led_18 (.in(mxl_led_ctrl[3]));
  mem_xfer mxl (
    .led_ctrl(mxl_led_ctrl), .rhs(rhs), .addr(addr_lo), .led_val(mxl_led_val), .read_mem(mxl_read_mem_reset),
    .write_lhs(mxl_write_rhs), .write_rhs(1'b1), .write_addr(mx_write_addr), .mem(mem));  // open: lhs
  LED led_19 (.in(instruction[7]));
  instruction_register ir (.led_ctrl(ir_led_ctrl), .out(instruction), .read_mem(ir_read_mem_reset), .mem(mem));
  timer_control_unit tcu (.led_end(tcu_led_end), .out(seq), .clk(clk_t), .reset(reset), .end_seq(tcu_end_seq));
  LED led_20 (.in(mem_bridge_led_ctrl[1]));
  LED led_21 (.in(mem_bridge_led_ctrl[0]));
  LED led_22 (.in(mxh_led_val[7]));
  LED led_23 (.in(mxh_led_val[6]));
  LED led_24 (.in(mxh_led_val[5]));
  LED led_25 (.in(mxh_led_val[4]));
  LED led_26 (.in(mxl_led_val[7]));
  LED led_27 (.in(mxl_led_val[6]));
  LED led_28 (.in(mxl_led_val[5]));
  LED led_29 (.in(mxl_led_val[4]));
  LED led_30 (.in(instruction[6]));
  LED led_31 (.in(instruction[5]));
  LED led_32 (.in(instruction[4]));
  LED led_33 (.in(instruction[3]));
  LED led_34 (.in(seq[2]));
  LED led_35 (.in(seq[1]));
  LED led_36 (.in(mxh_led_val[3]));
  LED led_37 (.in(mxh_led_val[2]));
  LED led_38 (.in(mxh_led_val[1]));
  LED led_39 (.in(mxh_led_val[0]));
  LED led_40 (.in(mxl_led_val[3]));
  LED led_41 (.in(mxl_led_val[2]));
  LED led_42 (.in(mxl_led_val[1]));
  LED led_43 (.in(mxl_led_val[0]));
  LED led_44 (.in(instruction[2]));
  LED led_45 (.in(instruction[1]));
  LED led_46 (.in(instruction[0]));
  LED led_47 (.in(seq[0]));
  LED led_48 (.in(ir_led_ctrl));
  LED led_49 (.in(tcu_led_end));
  Reset reset_2 (.out(reset_2_out));
  not not_1 (not_1_out, reset_2_out);
  LED led_50 (.in(data[7]));
  LED led_51 (.in(data[6]));
  LED led_52 (.in(data[5]));
  LED led_53 (.in(data[4]));
  LED led_54 (.in(data[3]));
  LED led_55 (.in(data[2]));
  LED led_56 (.in(data[1]));
  LED led_57 (.in(data[0]));
  or or_1 (reset_t, in_2, not_1_out);
  LED led_58 (.in(a_led_ctrl[0]));
  LED led_59 (.in(b_led_ctrl[0]));
  LED led_60 (.in(c_led_ctrl[0]));
  LED led_61 (.in(d_led_ctrl[0]));
  LED led_62 (.in(a_led_ctrl[1]));
  LED led_63 (.in(a_led_ctrl[2]));
  LED led_64 (.in(a_led_val[7]));
  gpr a (
    .led_ctrl(a_led_ctrl), .lhs(lhs), .rhs(rhs), .led_val(a_led_val), .read_data(a_read_data_reset),
    .write_lhs(a_write_lhs), .write_rhs(a_write_rhs), .data(data));
  LED led_65 (.in(b_led_ctrl[1]));
  LED led_66 (.in(b_led_ctrl[2]));
  LED led_67 (.in(b_led_val[7]));
  gpr b (
    .led_ctrl(b_led_ctrl), .lhs(lhs), .rhs(rhs), .led_val(b_led_val), .read_data(b_read_data_reset),
    .write_lhs(b_write_lhs), .write_rhs(b_write_rhs), .data(data));
  LED led_68 (.in(c_led_ctrl[1]));
  LED led_69 (.in(c_led_ctrl[2]));
  LED led_70 (.in(c_led_val[7]));
  gpr c (
    .led_ctrl(c_led_ctrl), .lhs(lhs), .rhs(rhs), .led_val(c_led_val), .read_data(c_read_data_reset),
    .write_lhs(c_write_lhs), .write_rhs(c_write_rhs), .data(data));
  LED led_71 (.in(d_led_ctrl[1]));
  LED led_72 (.in(d_led_ctrl[2]));
  LED led_73 (.in(d_led_val[7]));
  gpr d (
    .led_ctrl(d_led_ctrl), .lhs(lhs), .rhs(rhs), .led_val(d_led_val), .read_data(d_read_data_reset),
    .write_lhs(d_write_lhs), .write_rhs(d_write_rhs), .data(data));
  LED led_74 (.in(a_led_val[6]));
  LED led_75 (.in(a_led_val[5]));
  LED led_76 (.in(a_led_val[4]));
  LED led_77 (.in(a_led_val[3]));
  LED led_78 (.in(b_led_val[6]));
  LED led_79 (.in(b_led_val[5]));
  LED led_80 (.in(b_led_val[4]));
  LED led_81 (.in(b_led_val[3]));
  LED led_82 (.in(c_led_val[6]));
  LED led_83 (.in(c_led_val[5]));
  LED led_84 (.in(c_led_val[4]));
  LED led_85 (.in(c_led_val[3]));
  LED led_86 (.in(d_led_val[6]));
  LED led_87 (.in(d_led_val[5]));
  LED led_88 (.in(d_led_val[4]));
  LED led_89 (.in(d_led_val[3]));
  LED led_90 (.in(alu_1_p7));
  LED led_91 (.in(a_led_val[2]));
  LED led_92 (.in(a_led_val[1]));
  LED led_93 (.in(a_led_val[0]));
  LED led_94 (.in(b_led_val[2]));
  LED led_95 (.in(b_led_val[1]));
  LED led_96 (.in(b_led_val[0]));
  LED led_97 (.in(c_led_val[2]));
  LED led_98 (.in(c_led_val[1]));
  LED led_99 (.in(c_led_val[0]));
  LED led_100 (.in(d_led_val[2]));
  LED led_101 (.in(d_led_val[1]));
  LED led_102 (.in(d_led_val[0]));
  LED led_103 (.in(alu_op[4]));
  LED led_104 (.in(alu_op[3]));
  LED led_105 (.in(alu_op[2]));
  LED led_106 (.in(flags[4]));
  LED led_107 (.in(alu_op[1]));
  LED led_108 (.in(alu_op[0]));
  // alu alu_1: pin names not known; wires that end beside it: alu_1_p1, alu_write_data, lhs, rhs, alu_op, alu_1_p1, alu_1_p7, data, flags
  LED led_109 (.in(flags[0]));
  LED led_110 (.in(flags[1]));
  LED led_111 (.in(flags[2]));
  LED led_112 (.in(flags[3]));
  LED led_113 (.in(lhs[7]));
  LED led_114 (.in(lhs[6]));
  LED led_115 (.in(lhs[5]));
  LED led_116 (.in(lhs[4]));
  LED led_117 (.in(lhs[3]));
  LED led_118 (.in(lhs[2]));
  LED led_119 (.in(lhs[1]));
  LED led_120 (.in(lhs[0]));
  LED led_121 (.in(data[7]));
  LED led_122 (.in(data[6]));
  LED led_123 (.in(data[5]));
  LED led_124 (.in(rhs[7]));
  LED led_125 (.in(rhs[6]));
  LED led_126 (.in(rhs[5]));
  LED led_127 (.in(rhs[4]));
  LED led_128 (.in(rhs[3]));
  LED led_129 (.in(rhs[2]));
  LED led_130 (.in(rhs[1]));
  LED led_131 (.in(rhs[0]));
  LED led_132 (.in(data[4]));
  LED led_133 (.in(data[3]));
  LED led_134 (.in(data[2]));
  LED led_135 (.in(data[1]));
  LED led_136 (.in(data[0]));
  LED led_137 (.in(ra_p9[0]));
  LED led_138 (.in(ra_p9[1]));
  // return_address_register ra: pin names not known; wires that end beside it: lhs, rhs, ra_read_lhs, ra_read_rhs, ra_write_lhs, ra_write_rhs, clk, pc_out, ra_p9, rhs, ra_p11, lhs
  LED led_139 (.in(pc_p12[0]));
  LED led_140 (.in(pc_p12[1]));
  // program_counter_register pc: pin names not known; wires that end beside it: pc_inc, pc_dec, pc_read_lrhs, pc_write_addr, ra_read_pc, reset_t, clk, lhs, rhs, addr, pc_out, pc_p12, pc_p13
  LED led_141 (.in(sp_led_ctrl[0]));
  LED led_142 (.in(sp_led_ctrl[1]));
  counter_register sp (
    .inc(sp_inc), .dec(sp_dec), .read(sp_read_lrhs), .write(sp_write_addr), .reset(reset_t), .latch(clk),
    .lhs(lhs), .rhs(rhs), .addr(addr), .led_count(sp_led_count), .led_ctrl(sp_led_ctrl));
  LED led_143 (.in(si_led_ctrl[0]));
  LED led_144 (.in(si_led_ctrl[1]));
  counter_register si (
    .inc(si_inc), .dec(si_dec), .read(si_read_lrhs), .write(si_write_addr), .reset(reset_t), .latch(clk),
    .lhs(lhs), .rhs(rhs), .addr(addr), .led_count(si_led_count), .led_ctrl(si_led_ctrl));
  LED led_145 (.in(ra_p11[15]));
  LED led_146 (.in(ra_p9[2]));
  LED led_147 (.in(ra_p9[3]));
  LED led_148 (.in(pc_p13[15]));
  LED led_149 (.in(pc_p12[2]));
  LED led_150 (.in(pc_p12[3]));
  LED led_151 (.in(sp_led_count[15]));
  LED led_152 (.in(sp_led_ctrl[2]));
  LED led_153 (.in(sp_led_ctrl[3]));
  LED led_154 (.in(si_led_count[15]));
  LED led_155 (.in(si_led_ctrl[2]));
  LED led_156 (.in(si_led_ctrl[3]));
  LED led_157 (.in(axh_led_ctrl[0]));
  LED led_158 (.in(axh_led_ctrl[1]));
  addr_xfer axh (.read_addr(ax_read_addr), .tx(axh_write_lhs), .addr(addr_hi), .led_ctrl(axh_led_ctrl), .out(lhs));
  LED led_159 (.in(axl_led_ctrl[0]));
  LED led_160 (.in(axl_led_ctrl[1]));
  addr_xfer axl (.read_addr(ax_read_addr), .tx(axl_write_rhs), .addr(addr_lo), .led_ctrl(axl_led_ctrl), .out(rhs));
  LED led_161 (.in(ra_p11[14]));
  LED led_162 (.in(ra_p11[13]));
  LED led_163 (.in(ra_p11[12]));
  LED led_164 (.in(ra_p11[11]));
  LED led_165 (.in(pc_p13[14]));
  LED led_166 (.in(pc_p13[13]));
  LED led_167 (.in(pc_p13[12]));
  LED led_168 (.in(pc_p13[11]));
  LED led_169 (.in(sp_led_count[14]));
  LED led_170 (.in(sp_led_count[13]));
  LED led_171 (.in(sp_led_count[12]));
  LED led_172 (.in(sp_led_count[11]));
  LED led_173 (.in(si_led_count[14]));
  LED led_174 (.in(si_led_count[13]));
  LED led_175 (.in(si_led_count[12]));
  LED led_176 (.in(si_led_count[11]));
  LED led_177 (.in(lhs[7]));
  LED led_178 (.in(lhs[6]));
  LED led_179 (.in(lhs[5]));
  LED led_180 (.in(rhs[7]));
  LED led_181 (.in(rhs[6]));
  LED led_182 (.in(rhs[5]));
  LED led_183 (.in(ra_p11[10]));
  LED led_184 (.in(ra_p11[9]));
  LED led_185 (.in(ra_p11[8]));
  LED led_186 (.in(ra_p11[7]));
  LED led_187 (.in(pc_p13[10]));
  LED led_188 (.in(pc_p13[9]));
  LED led_189 (.in(pc_p13[8]));
  LED led_190 (.in(pc_p13[7]));
  LED led_191 (.in(sp_led_count[10]));
  LED led_192 (.in(sp_led_count[9]));
  LED led_193 (.in(sp_led_count[8]));
  LED led_194 (.in(sp_led_count[7]));
  LED led_195 (.in(si_led_count[10]));
  LED led_196 (.in(si_led_count[9]));
  LED led_197 (.in(si_led_count[8]));
  LED led_198 (.in(si_led_count[7]));
  LED led_199 (.in(lhs[4]));
  LED led_200 (.in(lhs[3]));
  LED led_201 (.in(lhs[2]));
  LED led_202 (.in(lhs[1]));
  LED led_203 (.in(rhs[4]));
  LED led_204 (.in(rhs[3]));
  LED led_205 (.in(rhs[2]));
  LED led_206 (.in(rhs[1]));
  LED led_207 (.in(ra_p11[6]));
  LED led_208 (.in(ra_p11[5]));
  LED led_209 (.in(ra_p11[4]));
  LED led_210 (.in(ra_p11[3]));
  LED led_211 (.in(pc_p13[6]));
  LED led_212 (.in(pc_p13[5]));
  LED led_213 (.in(pc_p13[4]));
  LED led_214 (.in(pc_p13[3]));
  LED led_215 (.in(sp_led_count[6]));
  LED led_216 (.in(sp_led_count[5]));
  LED led_217 (.in(sp_led_count[4]));
  LED led_218 (.in(sp_led_count[3]));
  LED led_219 (.in(si_led_count[6]));
  LED led_220 (.in(si_led_count[5]));
  LED led_221 (.in(si_led_count[4]));
  LED led_222 (.in(si_led_count[3]));
  LED led_223 (.in(lhs[0]));
  LED led_224 (.in(rhs[0]));
  LED led_225 (.in(ra_p11[2]));
  LED led_226 (.in(ra_p11[1]));
  LED led_227 (.in(ra_p11[0]));
  LED led_228 (.in(pc_p13[2]));
  LED led_229 (.in(pc_p13[1]));
  LED led_230 (.in(pc_p13[0]));
  LED led_231 (.in(sp_led_count[2]));
  LED led_232 (.in(sp_led_count[1]));
  LED led_233 (.in(sp_led_count[0]));
  LED led_234 (.in(si_led_count[2]));
  LED led_235 (.in(si_led_count[1]));
  LED led_236 (.in(si_led_count[0]));
  LED led_237 (.in(addr[15]));
  LED led_238 (.in(addr[14]));
  LED led_239 (.in(addr[13]));
  LED led_240 (.in(addr[12]));
  LED led_241 (.in(addr[11]));
  LED led_242 (.in(addr[10]));
  LED led_243 (.in(addr[9]));
  LED led_244 (.in(addr[8]));
  LED led_245 (.in(addr[7]));
  LED led_246 (.in(addr[6]));
  LED led_247 (.in(addr[5]));
  LED led_248 (.in(addr[4]));
  LED led_249 (.in(addr[3]));
  LED led_250 (.in(addr[2]));
  LED led_251 (.in(addr[1]));
  LED led_252 (.in(addr[0]));
endmodule
