// Digital circuit addr_xfer.dig as structural Verilog
module addr_xfer (
  input  [7:0] addr,
  input  tx,
  input  read_addr,
  output [7:0] out,
  output [1:0] led_ctrl
);

  wire delay_1_out, delay_2_out, delay_3_out, delay_4_out, delay_5_out, delay_6_out, delay_7_out,
       delay_8_out, Q0, Q1, Q2, Q3, Q4, Q5, Q6, Q7;

  Delay delay_1 (.in(Q0), .out(delay_1_out));
  Delay delay_2 (.in(Q1), .out(delay_2_out));
  Delay delay_3 (.in(Q2), .out(delay_3_out));
  Delay delay_4 (.in(Q3), .out(delay_4_out));
  Delay delay_5 (.in(Q4), .out(delay_5_out));
  Delay delay_6 (.in(Q5), .out(delay_6_out));
  Delay delay_7 (.in(Q6), .out(delay_7_out));
  Delay delay_8 (.in(Q7), .out(delay_8_out));
  not not_1 (led_ctrl[0], read_addr);
  not not_2 (led_ctrl[1], tx);
  _74574 _74574_1 (
    .pin1(1'b0), .pin2(addr[0]), .pin3(addr[1]), .pin4(addr[2]), .pin5(addr[3]), .pin6(addr[4]),
    .pin7(addr[5]), .pin8(addr[6]), .pin9(addr[7]), .pin10(1'b0), .pin11(read_addr), .pin12(Q7), .pin13(Q6),
    .pin14(Q5), .pin15(Q4), .pin16(Q3), .pin17(Q2), .pin18(Q1), .pin19(Q0), .pin20(1'b1));
  _74541 _74541_1 (
    .pin1(tx), .pin2(delay_1_out), .pin3(delay_2_out), .pin4(delay_3_out), .pin5(delay_4_out),
    .pin6(delay_5_out), .pin7(delay_6_out), .pin8(delay_7_out), .pin9(delay_8_out), .pin10(1'b0),
    .pin11(out[7]), .pin12(out[6]), .pin13(out[5]), .pin14(out[4]), .pin15(out[3]), .pin16(out[2]),
    .pin17(out[1]), .pin18(out[0]), .pin19(1'b0), .pin20(1'b1));

  // Other names for the same wires on the sheet: A0 = addr[0]; A1 = addr[1]; A2 = addr[2]; A3 = addr[3]; A4 = addr[4];
  //   A5 = addr[5]; A6 = addr[6]; A7 = addr[7]; LOAD = read_addr; RHS_0 = out[0]; RHS_1 = out[1]; RHS_2 = out[2];
  //   RHS_3 = out[3]; RHS_4 = out[4]; RHS_5 = out[5]; RHS_6 = out[6]; RHS_7 = out[7]
endmodule
