// Digital circuit alu.dig as structural Verilog
module alu (
  input  [7:0] lhs,
  input  [7:0] rhs,
  input  [4:0] alu_op,
  input  alu_write_data,
  output [7:0] result,
  output [4:0] flags,
  output led_ctrl
);

  wire not_2_out;
  wire [15:13] eeprom_1_d;

  not not_1 (led_ctrl, alu_write_data);
  not not_2 (not_2_out, alu_write_data);
  EEPROM #(.AddrBits(21), .Bits(16)) eeprom_1 (
    .A({alu_op, lhs, rhs}), .CS(not_2_out), .WE(1'b0), .OE(1'b1), .D({eeprom_1_d, flags, result}));

  // Other names for the same wires on the sheet: data_0 = result[0]; data_1 = result[1]; data_2 = result[2];
  //   data_3 = result[3]; data_4 = result[4]; data_5 = result[5]; data_6 = result[6]; data_7 = result[7];
  //   C = flags[0]; Z = flags[1]; S = flags[2]; V = flags[3]; D = flags[4]; alu_op_0 = alu_op[0];
  //   alu_op_1 = alu_op[1]; alu_op_2 = alu_op[2]; alu_op_3 = alu_op[3]; alu_op_4 = alu_op[4]; LHS_0 = lhs[0];
  //   LHS_1 = lhs[1]; LHS_2 = lhs[2]; LHS_3 = lhs[3]; LHS_4 = lhs[4]; LHS_5 = lhs[5]; LHS_6 = lhs[6]; LHS_7 = lhs[7];
  //   RHS_0 = rhs[0]; RHS_1 = rhs[1]; RHS_2 = rhs[2]; RHS_3 = rhs[3]; RHS_4 = rhs[4]; RHS_5 = rhs[5]; RHS_6 = rhs[6];
  //   RHS_7 = rhs[7]
endmodule
