// Digital circuit bus_controller.dig as structural Verilog
module bus_controller (
  input  [15:0] decoder_in0,
  input  [15:0] decoder_in1,
  input  clk,
  output [60:0] out,
  output [4:0] alu_op
);

  wire a_readdata, a_writelhs, a_writerhs, alu_writedata, ax_read_addr, axh_writelhs, axl_writerhs,
       b_readdata, b_writelhs, b_writerhs, c_readdata, c_writelhs, c_writerhs, d_readdata, d_writelhs,
       d_writerhs, device0_readdata, device0_writedata, device1_readdata, device1_writedata,
       device2_readdata, device2_writedata, device3_readdata, device3_writedata, device4_readdata,
       device4_writedata, device5_readdata, device6_readdata, device7_readdata, device8_readdata,
       device9_readdata, device10_readdata, ir_read_mem, mb_writedata, mb_writemem, mem_out, mx_write_addr,
       mxh_read_mem, mxh_writelhs, mxl_read_mem, mxl_writerhs, pc_dec, pc_inc, pc_read_lrhs, pc_write_addr,
       pc_write_ra, ra_read_lhs, ra_read_pc, ra_read_rhs, ra_writelhs, ra_writerhs, ram_write, rti, si_dec,
       si_inc, si_read_lrhs, si_write_addr, sp_dec, sp_inc, sp_read_lrhs, sp_write_addr, tcu_endseq;

  _74138 mem_write (
    .pin1(decoder_in0[0]), .pin2(decoder_in0[1]), .pin3(1'b0), .pin4(1'b0), .pin5(1'b0), .pin6(1'b1),
    .pin8(1'b0), .pin13(mb_writemem), .pin14(mem_out), .pin16(1'b1));  // open: pin7, pin9, pin10, pin11, pin12, pin15
  _74138 mem_read (
    .pin1(decoder_in0[2]), .pin2(decoder_in0[3]), .pin3(1'b0), .pin4(1'b0), .pin5(clk), .pin6(1'b1),
    .pin8(1'b0), .pin12(mxl_read_mem), .pin13(mxh_read_mem), .pin14(ir_read_mem), .pin16(1'b1));  // open: pin7, pin9, pin10, pin11, pin15
  _74138 data_write (
    .pin1(decoder_in0[4]), .pin2(decoder_in0[5]), .pin3(decoder_in0[6]), .pin4(1'b0), .pin5(1'b0),
    .pin6(1'b1), .pin7(device4_writedata), .pin8(1'b0), .pin9(device3_writedata), .pin10(device2_writedata),
    .pin11(device1_writedata), .pin12(device0_writedata), .pin13(alu_writedata), .pin14(mb_writedata),
    .pin16(1'b1));  // open: pin15
  _74138 data_read_lo (
    .pin1(decoder_in0[7]), .pin2(decoder_in0[8]), .pin3(decoder_in0[9]), .pin4(decoder_in0[10]), .pin5(clk),
    .pin6(1'b1), .pin7(device2_readdata), .pin8(1'b0), .pin9(device1_readdata), .pin10(device0_readdata),
    .pin11(d_readdata), .pin12(c_readdata), .pin13(b_readdata), .pin14(a_readdata), .pin16(1'b1));  // open: pin15
  _74138 lhs_write (
    .pin1(decoder_in0[11]), .pin2(decoder_in0[12]), .pin3(decoder_in0[13]), .pin4(1'b0), .pin5(1'b0),
    .pin6(1'b1), .pin7(axh_writelhs), .pin8(1'b0), .pin9(ra_writelhs), .pin10(d_writelhs),
    .pin11(c_writelhs), .pin12(b_writelhs), .pin13(a_writelhs), .pin14(mxh_writelhs), .pin16(1'b1));  // open: pin15
  _74138 data_read_hi (
    .pin1(decoder_in0[7]), .pin2(decoder_in0[8]), .pin3(decoder_in0[9]), .pin4(1'b0), .pin5(clk),
    .pin6(decoder_in0[10]), .pin7(device10_readdata), .pin8(1'b0), .pin9(device9_readdata),
    .pin10(device8_readdata), .pin11(device7_readdata), .pin12(device6_readdata), .pin13(device5_readdata),
    .pin14(device4_readdata), .pin15(device3_readdata), .pin16(1'b1));
  _74138 rhs_write (
    .pin1(decoder_in0[14]), .pin2(decoder_in0[15]), .pin3(decoder_in1[0]), .pin4(1'b0), .pin5(1'b0),
    .pin6(1'b1), .pin7(axl_writerhs), .pin8(1'b0), .pin9(ra_writerhs), .pin10(d_writerhs),
    .pin11(c_writerhs), .pin12(b_writerhs), .pin13(a_writerhs), .pin14(mxl_writerhs), .pin16(1'b1));  // open: pin15
  _74138 lrhs_read (
    .pin1(decoder_in1[1]), .pin2(decoder_in1[2]), .pin3(1'b0), .pin4(1'b0), .pin5(clk), .pin6(1'b1),
    .pin8(1'b0), .pin12(si_read_lrhs), .pin13(sp_read_lrhs), .pin14(pc_read_lrhs), .pin16(1'b1));  // open: pin7, pin9, pin10, pin11, pin15
  _74138 addr_write (
    .pin1(decoder_in1[3]), .pin2(decoder_in1[4]), .pin3(1'b0), .pin4(1'b0), .pin5(1'b0), .pin6(1'b1),
    .pin8(1'b0), .pin12(si_write_addr), .pin13(sp_write_addr), .pin14(mx_write_addr), .pin15(pc_write_addr),
    .pin16(1'b1));  // open: pin7, pin9, pin10, pin11
  _74138 inc_dec_sto (
    .pin1(decoder_in1[5]), .pin2(decoder_in1[6]), .pin3(decoder_in1[7]), .pin4(1'b0), .pin5(clk),
    .pin6(1'b1), .pin7(pc_write_ra), .pin8(1'b0), .pin9(ram_write), .pin10(si_dec), .pin11(sp_dec),
    .pin12(si_inc), .pin13(sp_inc), .pin14(pc_dec), .pin16(1'b1));  // open: pin15
  _74138 seq (
    .pin1(decoder_in1[8]), .pin2(decoder_in1[9]), .pin3(decoder_in1[10]), .pin4(1'b0), .pin5(clk),
    .pin6(1'b1), .pin7(ax_read_addr), .pin8(1'b0), .pin9(ra_read_pc), .pin10(ra_read_rhs),
    .pin11(ra_read_lhs), .pin12(rti), .pin13(tcu_endseq), .pin14(pc_inc), .pin16(1'b1));  // open: pin15
  Delay #(.Bits(61)) delay_1 (
    .in({ax_read_addr, ra_read_pc, ra_read_rhs, ra_read_lhs, rti, tcu_endseq, pc_inc, ram_write, si_dec, sp_dec, si_inc, sp_inc, pc_dec, si_write_addr, sp_write_addr, pc_write_addr, mx_write_addr, si_read_lrhs, sp_read_lrhs, pc_read_lrhs, axl_writerhs, ra_writerhs, d_writerhs, c_writerhs, b_writerhs, a_writerhs, mxl_writerhs, axh_writelhs, ra_writelhs, d_writelhs, c_writelhs, b_writelhs, a_writelhs, mxh_writelhs, device10_readdata, device9_readdata, device8_readdata, device7_readdata, device6_readdata, device5_readdata, device4_readdata, device3_readdata, device2_readdata, device1_readdata, device0_readdata, d_readdata, c_readdata, b_readdata, a_readdata, device4_writedata, device3_writedata, device2_writedata, device1_writedata, device0_writedata, alu_writedata, mb_writedata, mxl_read_mem, mxh_read_mem, ir_read_mem, mb_writemem, mem_out}),
    .out(out));

  assign alu_op = decoder_in1[15:11];

  // Other names for the same wires on the sheet: mem_write_0 = decoder_in0[0]; mem_write_1 = decoder_in0[1];
  //   mem_read_0 = decoder_in0[2]; mem_read_1 = decoder_in0[3]; data_write_0 = decoder_in0[4];
  //   data_write_1 = decoder_in0[5]; data_write_2 = decoder_in0[6]; data_read_0 = decoder_in0[7];
  //   data_read_1 = decoder_in0[8]; data_read_2 = decoder_in0[9]; data_read_3 = decoder_in0[10];
  //   lhs_write_0 = decoder_in0[11]; lhs_write_1 = decoder_in0[12]; lhs_write_2 = decoder_in0[13];
  //   rhs_write_0 = decoder_in0[14]; rhs_write_1 = decoder_in0[15]; rhs_write_2 = decoder_in1[0];
  //   lrhs_read_0 = decoder_in1[1]; lrhs_read_1 = decoder_in1[2]; addr_write_0 = decoder_in1[3];
  //   addr_write_1 = decoder_in1[4]; incdecsto_0 = decoder_in1[5]; incdecsto_1 = decoder_in1[6];
  //   incdecsto_2 = decoder_in1[7]; seq_0 = decoder_in1[8]; seq_1 = decoder_in1[9]; seq_2 = decoder_in1[10];
  //   alu_op_0 = decoder_in1[11]; alu_op_1 = decoder_in1[12]; alu_op_2 = decoder_in1[13]; alu_op_3 = decoder_in1[14];
  //   alu_op_4 = decoder_in1[15]
endmodule
