// Digital circuit decoder_0.dig as structural Verilog
module decoder_0 (
  input  [4:0] flags_in,
  input  [7:0] ir_in,
  input  [2:0] tcu_in,
  output [15:0] data
);

  wire [15:0] data_t;

  EEPROM #(.AddrBits(16), .Bits(16)) eeprom_1 (
    .A({flags_in, ir_in, tcu_in}), .CS(1'b1), .WE(1'b0), .OE(1'b1), .D(data_t));
  Delay #(.Bits(16), .delayTime(2)) delay_1 (.in(data_t), .out(data));

  // Other names for the same wires on the sheet: decode_hi[4:0] = flags_in;
  //   decode_in[15:0] = {flags_in, ir_in, tcu_in}; decode_lo[2:0] = tcu_in; decode_mid[7:0] = ir_in

  // Notes on the sheet:
  //   contents of eeprom_1 (hex, n*v repeats v):
  //   5,7*0,5,91,6*0,5,111,6*0,5,191,6*0,5,211,6*0,5,d,6*0,5,9,6*0,5
  //   ,1200,6*0,5,100e,6*0,5,100d,a00
endmodule
