// Digital circuit gpr.dig as structural Verilog
module gpr (
  input  read_data,
  input  write_lhs,
  input  write_rhs,
  input  [7:0] data,
  output [7:0] led_val,
  output [7:0] lhs,
  output [7:0] rhs,
  output [2:0] led_ctrl
);

  wire _74574_1_pin12, _74574_1_pin13, _74574_1_pin14, _74574_1_pin15, _74574_1_pin16, _74574_1_pin17,
       _74574_1_pin18, _74574_1_pin19;

  _74574 _74574_1 (
    .pin1(1'b0), .pin2(data[0]), .pin3(data[1]), .pin4(data[2]), .pin5(data[3]), .pin6(data[4]),
    .pin7(data[5]), .pin8(data[6]), .pin9(data[7]), .pin10(1'b0), .pin11(read_data), .pin12(_74574_1_pin12),
    .pin13(_74574_1_pin13), .pin14(_74574_1_pin14), .pin15(_74574_1_pin15), .pin16(_74574_1_pin16),
    .pin17(_74574_1_pin17), .pin18(_74574_1_pin18), .pin19(_74574_1_pin19), .pin20(1'b1));
  Delay delay_1 (.in(_74574_1_pin19), .out(led_val[0]));
  Delay delay_2 (.in(_74574_1_pin18), .out(led_val[1]));
  Delay delay_3 (.in(_74574_1_pin17), .out(led_val[2]));
  Delay delay_4 (.in(_74574_1_pin16), .out(led_val[3]));
  Delay delay_5 (.in(_74574_1_pin15), .out(led_val[4]));
  Delay delay_6 (.in(_74574_1_pin14), .out(led_val[5]));
  Delay delay_7 (.in(_74574_1_pin13), .out(led_val[6]));
  Delay delay_8 (.in(_74574_1_pin12), .out(led_val[7]));
  _74541 _74541_1 (
    .pin1(write_lhs), .pin2(led_val[0]), .pin3(led_val[1]), .pin4(led_val[2]), .pin5(led_val[3]),
    .pin6(led_val[4]), .pin7(led_val[5]), .pin8(led_val[6]), .pin9(led_val[7]), .pin10(1'b0), .pin11(lhs[7]),
    .pin12(lhs[6]), .pin13(lhs[5]), .pin14(lhs[4]), .pin15(lhs[3]), .pin16(lhs[2]), .pin17(lhs[1]),
    .pin18(lhs[0]), .pin19(1'b0), .pin20(1'b1));
  not not_1 (led_ctrl[0], read_data);
  not not_2 (led_ctrl[1], write_lhs);
  not not_3 (led_ctrl[2], write_rhs);
  _74541 _74541_2 (
    .pin1(write_rhs), .pin2(led_val[0]), .pin3(led_val[1]), .pin4(led_val[2]), .pin5(led_val[3]),
    .pin6(led_val[4]), .pin7(led_val[5]), .pin8(led_val[6]), .pin9(led_val[7]), .pin10(1'b0), .pin11(rhs[7]),
    .pin12(rhs[6]), .pin13(rhs[5]), .pin14(rhs[4]), .pin15(rhs[3]), .pin16(rhs[2]), .pin17(rhs[1]),
    .pin18(rhs[0]), .pin19(1'b0), .pin20(1'b1));

  // Other names for the same wires on the sheet: _1OUT_0 = lhs[0]; _1OUT_1 = lhs[1]; _1OUT_2 = lhs[2];
  //   _1OUT_3 = lhs[3]; _1OUT_4 = lhs[4]; _1OUT_5 = lhs[5]; _1OUT_6 = lhs[6]; _1OUT_7 = lhs[7]; _2OUT_0 = rhs[0];
  //   _2OUT_1 = rhs[1]; _2OUT_2 = rhs[2]; _2OUT_3 = rhs[3]; _2OUT_4 = rhs[4]; _2OUT_5 = rhs[5]; _2OUT_6 = rhs[6];
  //   _2OUT_7 = rhs[7]; D0 = data[0]; D1 = data[1]; D2 = data[2]; D3 = data[3]; D4 = data[4]; D5 = data[5];
  //   D6 = data[6]; D7 = data[7]; LOAD = read_data; Q0 = led_val[0]; Q1 = led_val[1]; Q2 = led_val[2];
  //   Q3 = led_val[3]; Q4 = led_val[4]; Q5 = led_val[5]; Q6 = led_val[6]; Q7 = led_val[7]; WRITE_1 = write_lhs;
  //   WRITE_2 = write_rhs
endmodule
