// Digital circuit instruction_register.dig as structural Verilog
module instruction_register (
  input  read_mem,
  input  [7:0] mem,
  output [7:0] out,
  output led_ctrl
);

  wire _74574_1_pin12, _74574_1_pin13, _74574_1_pin14, _74574_1_pin15, _74574_1_pin16, _74574_1_pin17,
       _74574_1_pin18, _74574_1_pin19;

  not not_1 (led_ctrl, read_mem);
  _74574 _74574_1 (
    .pin1(1'b0), .pin2(mem[0]), .pin3(mem[1]), .pin4(mem[2]), .pin5(mem[3]), .pin6(mem[4]), .pin7(mem[5]),
    .pin8(mem[6]), .pin9(mem[7]), .pin10(1'b0), .pin11(read_mem), .pin12(_74574_1_pin12),
    .pin13(_74574_1_pin13), .pin14(_74574_1_pin14), .pin15(_74574_1_pin15), .pin16(_74574_1_pin16),
    .pin17(_74574_1_pin17), .pin18(_74574_1_pin18), .pin19(_74574_1_pin19), .pin20(1'b1));
  Delay delay_1 (.in(_74574_1_pin19), .out(out[0]));
  Delay delay_2 (.in(_74574_1_pin18), .out(out[1]));
  Delay delay_3 (.in(_74574_1_pin17), .out(out[2]));
  Delay delay_4 (.in(_74574_1_pin16), .out(out[3]));
  Delay delay_5 (.in(_74574_1_pin15), .out(out[4]));
  Delay delay_6 (.in(_74574_1_pin14), .out(out[5]));
  Delay delay_7 (.in(_74574_1_pin13), .out(out[6]));
  Delay delay_8 (.in(_74574_1_pin12), .out(out[7]));

  // Other names for the same wires on the sheet: LOAD = read_mem; D0 = mem[0]; D1 = mem[1]; D2 = mem[2]; D3 = mem[3];
  //   D4 = mem[4]; D5 = mem[5]; D6 = mem[6]; D7 = mem[7]; Q0 = out[0]; Q1 = out[1]; Q2 = out[2]; Q3 = out[3];
  //   Q4 = out[4]; Q5 = out[5]; Q6 = out[6]; Q7 = out[7]
endmodule
