// Digital circuit mem_bridge.dig as structural Verilog
module mem_bridge (
  input  [7:0] data_in,
  input  [7:0] mem_in,
  input  write_mem,
  input  write_data,
  output [7:0] data_out,
  output [7:0] mem_out,
  output [1:0] led_ctrl
);

  wire DISABLE_data__gt_mem, DISABLE_mem__gt_data;

  not not_1 (led_ctrl[0], write_mem);
  not not_2 (led_ctrl[1], write_data);
  _7404 _7404_1 (
    .pin1(write_mem), .pin2(DISABLE_mem__gt_data), .pin3(write_data), .pin4(DISABLE_data__gt_mem),
    .pin5(1'b0), .pin7(1'b0), .pin9(1'b0), .pin11(1'b0), .pin13(1'b0), .pin14(1'b1));  // open: pin6, pin8, pin10, pin12
  _74541 _74541_1 (
    .pin1(write_mem), .pin2(data_in[0]), .pin3(data_in[1]), .pin4(data_in[2]), .pin5(data_in[3]),
    .pin6(data_in[4]), .pin7(data_in[5]), .pin8(data_in[6]), .pin9(data_in[7]), .pin10(1'b0),
    .pin11(mem_out[7]), .pin12(mem_out[6]), .pin13(mem_out[5]), .pin14(mem_out[4]), .pin15(mem_out[3]),
    .pin16(mem_out[2]), .pin17(mem_out[1]), .pin18(mem_out[0]), .pin19(DISABLE_data__gt_mem), .pin20(1'b1));
  _74541 _74541_2 (
    .pin1(write_data), .pin2(mem_in[0]), .pin3(mem_in[1]), .pin4(mem_in[2]), .pin5(mem_in[3]),
    .pin6(mem_in[4]), .pin7(mem_in[5]), .pin8(mem_in[6]), .pin9(mem_in[7]), .pin10(1'b0),
    .pin11(data_out[7]), .pin12(data_out[6]), .pin13(data_out[5]), .pin14(data_out[4]), .pin15(data_out[3]),
    .pin16(data_out[2]), .pin17(data_out[1]), .pin18(data_out[0]), .pin19(DISABLE_mem__gt_data), .pin20(1'b1));

  // Other names for the same wires on the sheet: data__gt_mem = write_mem; Din_0 = data_in[0]; Din_1 = data_in[1];
  //   Din_2 = data_in[2]; Din_3 = data_in[3]; Din_4 = data_in[4]; Din_5 = data_in[5]; Din_6 = data_in[6];
  //   Din_7 = data_in[7]; Dout_0 = data_out[0]; Dout_1 = data_out[1]; Dout_2 = data_out[2]; Dout_3 = data_out[3];
  //   Dout_4 = data_out[4]; Dout_5 = data_out[5]; Dout_6 = data_out[6]; Dout_7 = data_out[7];
  //   mem__gt_data = write_data; Min_0 = mem_in[0]; Min_1 = mem_in[1]; Min_2 = mem_in[2]; Min_3 = mem_in[3];
  //   Min_4 = mem_in[4]; Min_5 = mem_in[5]; Min_6 = mem_in[6]; Min_7 = mem_in[7]; Mout_0 = mem_out[0];
  //   Mout_1 = mem_out[1]; Mout_2 = mem_out[2]; Mout_3 = mem_out[3]; Mout_4 = mem_out[4]; Mout_5 = mem_out[5];
  //   Mout_6 = mem_out[6]; Mout_7 = mem_out[7]
endmodule
