// Digital circuit mem_xfer.dig as structural Verilog
module mem_xfer (
  input  read_mem,
  input  write_lhs,
  input  write_rhs,
  input  [7:0] mem,
  input  write_addr,
  output [7:0] led_val,
  output [7:0] lhs,
  output [7:0] rhs,
  output [3:0] led_ctrl,
  output [7:0] addr
);

  wire delay_1_out, delay_2_out, delay_3_out, delay_4_out, delay_5_out, delay_6_out, delay_7_out,
       delay_8_out, delay_9_out, delay_10_out, delay_11_out, delay_12_out, delay_13_out, delay_14_out,
       delay_15_out, delay_16_out, delay_17_out, delay_18_out, delay_19_out, delay_20_out, delay_21_out,
       delay_22_out, delay_23_out, delay_24_out;

  _74574 _74574_1 (
    .pin1(1'b0), .pin2(mem[0]), .pin3(mem[1]), .pin4(mem[2]), .pin5(mem[3]), .pin6(mem[4]), .pin7(mem[5]),
    .pin8(mem[6]), .pin9(mem[7]), .pin10(1'b0), .pin11(read_mem), .pin12(led_val[7]), .pin13(led_val[6]),
    .pin14(led_val[5]), .pin15(led_val[4]), .pin16(led_val[3]), .pin17(led_val[2]), .pin18(led_val[1]),
    .pin19(led_val[0]), .pin20(1'b1));
  Delay delay_1 (.in(led_val[0]), .out(delay_1_out));
  Delay delay_2 (.in(led_val[1]), .out(delay_2_out));
  Delay delay_3 (.in(led_val[2]), .out(delay_3_out));
  Delay delay_4 (.in(led_val[3]), .out(delay_4_out));
  Delay delay_5 (.in(led_val[4]), .out(delay_5_out));
  Delay delay_6 (.in(led_val[5]), .out(delay_6_out));
  Delay delay_7 (.in(led_val[6]), .out(delay_7_out));
  Delay delay_8 (.in(led_val[7]), .out(delay_8_out));
  _74541 _74541_1 (
    .pin1(write_lhs), .pin2(delay_1_out), .pin3(delay_2_out), .pin4(delay_3_out), .pin5(delay_4_out),
    .pin6(delay_5_out), .pin7(delay_6_out), .pin8(delay_7_out), .pin9(delay_8_out), .pin10(1'b0),
    .pin11(lhs[7]), .pin12(lhs[6]), .pin13(lhs[5]), .pin14(lhs[4]), .pin15(lhs[3]), .pin16(lhs[2]),
    .pin17(lhs[1]), .pin18(lhs[0]), .pin19(1'b0), .pin20(1'b1));
  not not_1 (led_ctrl[0], read_mem);
  not not_2 (led_ctrl[1], write_lhs);
  not not_3 (led_ctrl[2], write_rhs);
  not not_4 (led_ctrl[3], write_addr);
  Delay delay_9 (.in(led_val[0]), .out(delay_9_out));
  Delay delay_10 (.in(led_val[1]), .out(delay_10_out));
  Delay delay_11 (.in(led_val[2]), .out(delay_11_out));
  Delay delay_12 (.in(led_val[3]), .out(delay_12_out));
  Delay delay_13 (.in(led_val[4]), .out(delay_13_out));
  Delay delay_14 (.in(led_val[5]), .out(delay_14_out));
  Delay delay_15 (.in(led_val[6]), .out(delay_15_out));
  Delay delay_16 (.in(led_val[7]), .out(delay_16_out));
  Delay delay_17 (.in(led_val[0]), .out(delay_17_out));
  Delay delay_18 (.in(led_val[1]), .out(delay_18_out));
  Delay delay_19 (.in(led_val[2]), .out(delay_19_out));
  Delay delay_20 (.in(led_val[3]), .out(delay_20_out));
  Delay delay_21 (.in(led_val[4]), .out(delay_21_out));
  Delay delay_22 (.in(led_val[5]), .out(delay_22_out));
  Delay delay_23 (.in(led_val[6]), .out(delay_23_out));
  Delay delay_24 (.in(led_val[7]), .out(delay_24_out));
  _74541 _74541_2 (
    .pin1(write_rhs), .pin2(delay_9_out), .pin3(delay_10_out), .pin4(delay_11_out), .pin5(delay_12_out),
    .pin6(delay_13_out), .pin7(delay_14_out), .pin8(delay_15_out), .pin9(delay_16_out), .pin10(1'b0),
    .pin11(rhs[7]), .pin12(rhs[6]), .pin13(rhs[5]), .pin14(rhs[4]), .pin15(rhs[3]), .pin16(rhs[2]),
    .pin17(rhs[1]), .pin18(rhs[0]), .pin19(1'b0), .pin20(1'b1));
  _74541 _74541_3 (
    .pin1(write_addr), .pin2(delay_17_out), .pin3(delay_18_out), .pin4(delay_19_out), .pin5(delay_20_out),
    .pin6(delay_21_out), .pin7(delay_22_out), .pin8(delay_23_out), .pin9(delay_24_out), .pin10(1'b0),
    .pin11(addr[7]), .pin12(addr[6]), .pin13(addr[5]), .pin14(addr[4]), .pin15(addr[3]), .pin16(addr[2]),
    .pin17(addr[1]), .pin18(addr[0]), .pin19(1'b0), .pin20(1'b1));

  // Other names for the same wires on the sheet: _1OUT_0 = lhs[0]; _1OUT_1 = lhs[1]; _1OUT_2 = lhs[2];
  //   _1OUT_3 = lhs[3]; _1OUT_4 = lhs[4]; _1OUT_5 = lhs[5]; _1OUT_6 = lhs[6]; _1OUT_7 = lhs[7]; _2OUT_0 = rhs[0];
  //   _2OUT_1 = rhs[1]; _2OUT_2 = rhs[2]; _2OUT_3 = rhs[3]; _2OUT_4 = rhs[4]; _2OUT_5 = rhs[5]; _2OUT_6 = rhs[6];
  //   _2OUT_7 = rhs[7]; _3OUT_0 = addr[0]; _3OUT_1 = addr[1]; _3OUT_2 = addr[2]; _3OUT_3 = addr[3]; _3OUT_4 = addr[4];
  //   _3OUT_5 = addr[5]; _3OUT_6 = addr[6]; _3OUT_7 = addr[7]; LOAD = read_mem; D0 = mem[0]; D1 = mem[1]; D2 = mem[2];
  //   D3 = mem[3]; D4 = mem[4]; D5 = mem[5]; D6 = mem[6]; D7 = mem[7]; Q0 = led_val[0]; Q1 = led_val[1];
  //   Q2 = led_val[2]; Q3 = led_val[3]; Q4 = led_val[4]; Q5 = led_val[5]; Q6 = led_val[6]; Q7 = led_val[7];
  //   WRITE_1 = write_lhs; WRITE_2 = write_rhs; WRITE_3 = write_addr
endmodule
