// Digital circuit memory.dig as structural Verilog
module memory (
  input  [15:0] addr,
  input  mem_out,
  input  ram_write,
  input  reset,
  output [7:0] mem,
  output [1:0] led_ctrl
);

  wire not_3_out;

  not not_1 (led_ctrl[0], mem_out);
  not not_2 (led_ctrl[1], ram_write);
  not not_3 (not_3_out, mem_out);
  EEPROM #(.AddrBits(15), .isProgramMemory("true"), .Bits(8)) rom (
    .A(addr[14:0]), .CS(not_3_out), .WE(1'b0), .OE(reset), .D(mem));
  // Pins of 1 and 8 bits meet at mem
  // Pins of 8 and 16 bits meet at addr

  // Notes on the sheet:
  //   contents of rom (hex, n*v repeats v):
  //   0,1,1,2,80,1,2,2,40,1,4,2,20,1,8,2,10,1,10,2,8,1,20,2,4,1,40,2,2
  //   ,1,80,2,1,1,40,2,2,1,20,2,4,1,10,2,8,1,8,2,10,1,4,2,20,1,2,2,40
  //   ,1,1,2,80,3,aa,4,55,5,aa,6,55,5,55,6,aa
endmodule
