// Digital circuit program_counter_register.dig as structural Verilog
module program_counter_register (
  input  inc,
  input  dec,
  input  reset,
  input  read,
  input  write_addr,
  input  latch,
  input  [7:0] lhs,
  input  [7:0] rhs,
  input  write_ret,
  output [15:0] addr,
  output [15:0] led_count,
  output [3:0] led_ctrl,
  output [15:0] ra
);

  wire _74193_1_pin12, _74193_1_pin13, _74193_2_pin12, _74193_2_pin13, _74193_3_pin12, _74193_3_pin13,
       _74541_2_pin2, _74541_2_pin3, _74541_2_pin4, _74541_2_pin5, _74541_2_pin6, _74541_2_pin7,
       _74541_2_pin8, _74541_2_pin9, delay_1_out, delay_2_out, delay_3_out, delay_4_out, delay_5_out,
       delay_6_out, delay_7_out, delay_8_out, delay_9_out, delay_10_out, delay_11_out, delay_12_out,
       delay_13_out, delay_14_out, delay_15_out, delay_16_out, delay_17_out, delay_18_out, delay_19_out,
       delay_20_out, delay_21_out, delay_22_out, delay_23_out, delay_24_out;

  Delay #(.delayTime(2)) delay_1 (.in(led_count[0]), .out(delay_1_out));
  Delay #(.delayTime(2)) delay_2 (.in(led_count[1]), .out(delay_2_out));
  Delay #(.delayTime(2)) delay_3 (.in(led_count[2]), .out(delay_3_out));
  Delay #(.delayTime(2)) delay_4 (.in(led_count[3]), .out(delay_4_out));
  Delay #(.delayTime(2)) delay_5 (.in(led_count[4]), .out(delay_5_out));
  Delay #(.delayTime(2)) delay_6 (.in(led_count[5]), .out(delay_6_out));
  Delay #(.delayTime(2)) delay_7 (.in(led_count[6]), .out(delay_7_out));
  Delay #(.delayTime(2)) delay_8 (.in(led_count[7]), .out(delay_8_out));
  _74193 _74193_1 (
    .pin1(rhs[1]), .pin2(led_count[1]), .pin3(led_count[0]), .pin4(dec), .pin5(inc), .pin6(led_count[2]),
    .pin7(led_count[3]), .pin8(1'b0), .pin9(rhs[3]), .pin10(rhs[2]), .pin11(read), .pin12(_74193_1_pin12),
    .pin13(_74193_1_pin13), .pin14(reset), .pin15(rhs[0]), .pin16(1'b1));
  _74574 _74574_1 (
    .pin1(write_addr), .pin2(delay_1_out), .pin3(delay_2_out), .pin4(delay_3_out), .pin5(delay_4_out),
    .pin6(delay_5_out), .pin7(delay_6_out), .pin8(delay_7_out), .pin9(delay_8_out), .pin10(1'b0),
    .pin11(latch), .pin12(addr[7]), .pin13(addr[6]), .pin14(addr[5]), .pin15(addr[4]), .pin16(addr[3]),
    .pin17(addr[2]), .pin18(addr[1]), .pin19(addr[0]), .pin20(1'b1));
  not not_1 (led_ctrl[0], inc);
  not not_2 (led_ctrl[1], dec);
  not not_3 (led_ctrl[2], read);
  not not_4 (led_ctrl[3], write_addr);
  Delay #(.delayTime(2)) delay_9 (.in(led_count[8]), .out(delay_9_out));
  Delay #(.delayTime(2)) delay_10 (.in(led_count[9]), .out(delay_10_out));
  Delay #(.delayTime(2)) delay_11 (.in(led_count[10]), .out(delay_11_out));
  Delay #(.delayTime(2)) delay_12 (.in(led_count[11]), .out(delay_12_out));
  Delay #(.delayTime(2)) delay_13 (.in(led_count[12]), .out(delay_13_out));
  Delay #(.delayTime(2)) delay_14 (.in(led_count[13]), .out(delay_14_out));
  Delay #(.delayTime(2)) delay_15 (.in(led_count[14]), .out(delay_15_out));
  Delay #(.delayTime(2)) delay_16 (.in(led_count[15]), .out(delay_16_out));
  _74193 _74193_2 (
    .pin1(rhs[5]), .pin2(led_count[5]), .pin3(led_count[4]), .pin4(_74193_1_pin13), .pin5(_74193_1_pin12),
    .pin6(led_count[6]), .pin7(led_count[7]), .pin8(1'b0), .pin9(rhs[7]), .pin10(rhs[6]), .pin11(read),
    .pin12(_74193_2_pin12), .pin13(_74193_2_pin13), .pin14(reset), .pin15(rhs[4]), .pin16(1'b1));
  _74574 _74574_2 (
    .pin1(write_addr), .pin2(delay_9_out), .pin3(delay_10_out), .pin4(delay_11_out), .pin5(delay_12_out),
    .pin6(delay_13_out), .pin7(delay_14_out), .pin8(delay_15_out), .pin9(delay_16_out), .pin10(1'b0),
    .pin11(latch), .pin12(addr[15]), .pin13(addr[14]), .pin14(addr[13]), .pin15(addr[12]), .pin16(addr[11]),
    .pin17(addr[10]), .pin18(addr[9]), .pin19(addr[8]), .pin20(1'b1));
  Delay delay_17 (.in(led_count[0]), .out(delay_17_out));
  Delay delay_18 (.in(led_count[1]), .out(delay_18_out));
  Delay delay_19 (.in(led_count[2]), .out(delay_19_out));
  Delay delay_20 (.in(led_count[3]), .out(delay_20_out));
  Delay delay_21 (.in(led_count[4]), .out(delay_21_out));
  Delay delay_22 (.in(led_count[5]), .out(delay_22_out));
  Delay delay_23 (.in(led_count[6]), .out(delay_23_out));
  Delay delay_24 (.in(led_count[7]), .out(delay_24_out));
  _74193 _74193_3 (
    .pin1(lhs[1]), .pin2(led_count[9]), .pin3(led_count[8]), .pin4(_74193_2_pin13), .pin5(_74193_2_pin12),
    .pin6(led_count[10]), .pin7(led_count[11]), .pin8(1'b0), .pin9(lhs[3]), .pin10(lhs[2]), .pin11(read),
    .pin12(_74193_3_pin12), .pin13(_74193_3_pin13), .pin14(reset), .pin15(lhs[0]), .pin16(1'b1));
  _74541 _74541_1 (
    .pin1(write_ret), .pin2(delay_17_out), .pin3(delay_18_out), .pin4(delay_19_out), .pin5(delay_20_out),
    .pin6(delay_21_out), .pin7(delay_22_out), .pin8(delay_23_out), .pin9(delay_24_out), .pin10(1'b0),
    .pin11(ra[7]), .pin12(ra[6]), .pin13(ra[5]), .pin14(ra[4]), .pin15(ra[3]), .pin16(ra[2]), .pin17(ra[1]),
    .pin18(ra[0]), .pin19(1'b0), .pin20(1'b1));
  _74193 _74193_4 (
    .pin1(lhs[5]), .pin2(led_count[13]), .pin3(led_count[12]), .pin4(_74193_3_pin13), .pin5(_74193_3_pin12),
    .pin6(led_count[14]), .pin7(led_count[15]), .pin8(1'b0), .pin9(lhs[7]), .pin10(lhs[6]), .pin11(read),
    .pin14(reset), .pin15(lhs[4]), .pin16(1'b1));  // open: pin12, pin13
  _74541 _74541_2 (
    .pin1(write_ret), .pin2(_74541_2_pin2), .pin3(_74541_2_pin3), .pin4(_74541_2_pin4), .pin5(_74541_2_pin5),
    .pin6(_74541_2_pin6), .pin7(_74541_2_pin7), .pin8(_74541_2_pin8), .pin9(_74541_2_pin9), .pin10(1'b0),
    .pin11(ra[15]), .pin12(ra[14]), .pin13(ra[13]), .pin14(ra[12]), .pin15(ra[11]), .pin16(ra[10]),
    .pin17(ra[9]), .pin18(ra[8]), .pin19(1'b0), .pin20(1'b1));
  Delay delay_25 (.in(led_count[8]), .out(_74541_2_pin2));
  Delay delay_26 (.in(led_count[9]), .out(_74541_2_pin3));
  Delay delay_27 (.in(led_count[10]), .out(_74541_2_pin4));
  Delay delay_28 (.in(led_count[11]), .out(_74541_2_pin5));
  Delay delay_29 (.in(led_count[12]), .out(_74541_2_pin6));
  Delay delay_30 (.in(led_count[13]), .out(_74541_2_pin7));
  Delay delay_31 (.in(led_count[14]), .out(_74541_2_pin8));
  Delay delay_32 (.in(led_count[15]), .out(_74541_2_pin9));

  // Other names for the same wires on the sheet: _2OUT_0 = ra[0]; _2OUT_1 = ra[1]; _2OUT_2 = ra[2]; _2OUT_3 = ra[3];
  //   _2OUT_4 = ra[4]; _2OUT_5 = ra[5]; _2OUT_6 = ra[6]; _2OUT_7 = ra[7]; _2OUT_8 = ra[8]; _2OUT_9 = ra[9];
  //   _2OUT_10 = ra[10]; _2OUT_11 = ra[11]; _2OUT_12 = ra[12]; _2OUT_13 = ra[13]; _2OUT_14 = ra[14];
  //   _2OUT_15 = ra[15]; LHS_0 = lhs[0]; LHS_1 = lhs[1]; LHS_2 = lhs[2]; LHS_3 = lhs[3]; LHS_4 = lhs[4];
  //   LHS_5 = lhs[5]; LHS_6 = lhs[6]; LHS_7 = lhs[7]; OUT_0 = addr[0]; OUT_1 = addr[1]; OUT_2 = addr[2];
  //   OUT_3 = addr[3]; OUT_4 = addr[4]; OUT_5 = addr[5]; OUT_6 = addr[6]; OUT_7 = addr[7]; OUT_8 = addr[8];
  //   OUT_9 = addr[9]; OUT_10 = addr[10]; OUT_11 = addr[11]; OUT_12 = addr[12]; OUT_13 = addr[13]; OUT_14 = addr[14];
  //   OUT_15 = addr[15]; Q0 = led_count[0]; Q1 = led_count[1]; Q2 = led_count[2]; Q3 = led_count[3];
  //   Q4 = led_count[4]; Q5 = led_count[5]; Q6 = led_count[6]; Q7 = led_count[7]; Q8 = led_count[8];
  //   Q9 = led_count[9]; Q10 = led_count[10]; Q11 = led_count[11]; Q12 = led_count[12]; Q13 = led_count[13];
  //   Q14 = led_count[14]; Q15 = led_count[15]; RHS_0 = rhs[0]; RHS_1 = rhs[1]; RHS_2 = rhs[2]; RHS_3 = rhs[3];
  //   RHS_4 = rhs[4]; RHS_5 = rhs[5]; RHS_6 = rhs[6]; RHS_7 = rhs[7]; WRITE_1 = write_addr; WRITE_2 = write_ret
endmodule
