// Digital circuit reset.dig as structural Verilog
module reset (
  input  reset,
  input  mb_write_data,
  input  mxh_read_mem,
  input  mxl_read_mem,
  input  ir_read_mem,
  input  a_read_data,
  input  b_read_data,
  input  c_read_data,
  input  d_read_data,
  output mb_write_data_reset,
  output mxh_read_mem_reset,
  output mxl_read_mem_reset,
  output ir_read_mem_reset,
  output a_read_data_reset,
  output b_read_data_reset,
  output c_read_data_reset,
  output d_read_data_reset,
  output [7:0] mem
);

  _74541 _74541_1 (
    .pin1(reset), .pin2(1'b0), .pin3(1'b0), .pin4(1'b0), .pin5(1'b0), .pin6(1'b0), .pin7(1'b0), .pin8(1'b0),
    .pin9(1'b0), .pin10(1'b0), .pin11(mem[7]), .pin12(mem[6]), .pin13(mem[5]), .pin14(mem[4]),
    .pin15(mem[3]), .pin16(mem[2]), .pin17(mem[1]), .pin18(mem[0]), .pin19(1'b0), .pin20(1'b1));
  _7408 _7408_1 (
    .pin1(reset), .pin2(mb_write_data), .pin3(mb_write_data_reset), .pin4(reset), .pin5(mxh_read_mem),
    .pin6(mxh_read_mem_reset), .pin7(1'b0), .pin8(mxl_read_mem_reset), .pin9(reset), .pin10(mxl_read_mem),
    .pin11(ir_read_mem_reset), .pin12(reset), .pin13(ir_read_mem), .pin14(1'b1));
  _7408 _7408_2 (
    .pin1(reset), .pin2(a_read_data), .pin3(a_read_data_reset), .pin4(reset), .pin5(b_read_data),
    .pin6(b_read_data_reset), .pin7(1'b0), .pin8(c_read_data_reset), .pin9(reset), .pin10(c_read_data),
    .pin11(d_read_data_reset), .pin12(reset), .pin13(d_read_data), .pin14(1'b1));
endmodule
