// Digital circuit return_address_register.dig as structural Verilog
module return_address_register (
  input  [7:0] lhs,
  input  [7:0] rhs,
  input  [15:0] pc,
  input  READ_lhs,
  input  WRITE_lhs,
  input  WRITE_rhs,
  input  READ_rhs,
  input  latch,
  output [7:0] rhs_out,
  output [7:0] lhs_out,
  output [3:0] led_ctrl,
  output [15:0] led_val
);

  wire _7432_1_pin3, _7432_1_pin6, delay_1_out, delay_2_out, delay_3_out, delay_4_out, delay_5_out,
       delay_6_out, delay_7_out, delay_8_out, delay_9_out, delay_10_out, delay_11_out, delay_12_out,
       delay_13_out, delay_14_out, delay_15_out, delay_16_out, display;

  not not_1 (led_ctrl[0], READ_lhs);
  not not_2 (led_ctrl[1], READ_rhs);
  not not_3 (led_ctrl[2], WRITE_lhs);
  not not_4 (led_ctrl[3], WRITE_rhs);
  Delay #(.delayTime(2)) delay_1 (.in(led_val[0]), .out(delay_1_out));
  Delay #(.delayTime(2)) delay_2 (.in(led_val[1]), .out(delay_2_out));
  Delay #(.delayTime(2)) delay_3 (.in(led_val[2]), .out(delay_3_out));
  Delay #(.delayTime(2)) delay_4 (.in(led_val[3]), .out(delay_4_out));
  Delay #(.delayTime(2)) delay_5 (.in(led_val[4]), .out(delay_5_out));
  Delay #(.delayTime(2)) delay_6 (.in(led_val[5]), .out(delay_6_out));
  Delay #(.delayTime(2)) delay_7 (.in(led_val[6]), .out(delay_7_out));
  Delay #(.delayTime(2)) delay_8 (.in(led_val[7]), .out(delay_8_out));
  _74541 _74541_1 (
    .pin1(READ_lhs), .pin2(rhs[0]), .pin3(rhs[1]), .pin4(rhs[2]), .pin5(rhs[3]), .pin6(rhs[4]),
    .pin7(rhs[5]), .pin8(rhs[6]), .pin9(rhs[7]), .pin10(1'b0), .pin11(pc[7]), .pin12(pc[6]), .pin13(pc[5]),
    .pin14(pc[4]), .pin15(pc[3]), .pin16(pc[2]), .pin17(pc[1]), .pin18(pc[0]), .pin19(1'b0), .pin20(1'b1));
  _74574 _74574_1 (
    .pin1(display), .pin2(pc[0]), .pin3(pc[1]), .pin4(pc[2]), .pin5(pc[3]), .pin6(pc[4]), .pin7(pc[5]),
    .pin8(pc[6]), .pin9(pc[7]), .pin10(1'b0), .pin11(latch), .pin12(led_val[7]), .pin13(led_val[6]),
    .pin14(led_val[5]), .pin15(led_val[4]), .pin16(led_val[3]), .pin17(led_val[2]), .pin18(led_val[1]),
    .pin19(led_val[0]), .pin20(1'b1));
  _74541 _74541_2 (
    .pin1(WRITE_rhs), .pin2(delay_1_out), .pin3(delay_2_out), .pin4(delay_3_out), .pin5(delay_4_out),
    .pin6(delay_5_out), .pin7(delay_6_out), .pin8(delay_7_out), .pin9(delay_8_out), .pin10(1'b0),
    .pin11(rhs_out[7]), .pin12(rhs_out[6]), .pin13(rhs_out[5]), .pin14(rhs_out[4]), .pin15(rhs_out[3]),
    .pin16(rhs_out[2]), .pin17(rhs_out[1]), .pin18(rhs_out[0]), .pin19(1'b0), .pin20(1'b1));
  Delay #(.delayTime(2)) delay_9 (.in(led_val[8]), .out(delay_9_out));
  Delay #(.delayTime(2)) delay_10 (.in(led_val[9]), .out(delay_10_out));
  Delay #(.delayTime(2)) delay_11 (.in(led_val[10]), .out(delay_11_out));
  Delay #(.delayTime(2)) delay_12 (.in(led_val[11]), .out(delay_12_out));
  Delay #(.delayTime(2)) delay_13 (.in(led_val[12]), .out(delay_13_out));
  Delay #(.delayTime(2)) delay_14 (.in(led_val[13]), .out(delay_14_out));
  Delay #(.delayTime(2)) delay_15 (.in(led_val[14]), .out(delay_15_out));
  Delay #(.delayTime(2)) delay_16 (.in(led_val[15]), .out(delay_16_out));
  _74541 _74541_3 (
    .pin1(READ_lhs), .pin2(lhs[0]), .pin3(lhs[1]), .pin4(lhs[2]), .pin5(lhs[3]), .pin6(lhs[4]),
    .pin7(lhs[5]), .pin8(lhs[6]), .pin9(lhs[7]), .pin10(1'b0), .pin11(pc[15]), .pin12(pc[14]),
    .pin13(pc[13]), .pin14(pc[12]), .pin15(pc[11]), .pin16(pc[10]), .pin17(pc[9]), .pin18(pc[8]),
    .pin19(1'b0), .pin20(1'b1));
  _74574 _74574_2 (
    .pin1(display), .pin2(pc[8]), .pin3(pc[9]), .pin4(pc[10]), .pin5(pc[11]), .pin6(pc[12]), .pin7(pc[13]),
    .pin8(pc[14]), .pin9(pc[15]), .pin10(1'b0), .pin11(latch), .pin12(led_val[15]), .pin13(led_val[14]),
    .pin14(led_val[13]), .pin15(led_val[12]), .pin16(led_val[11]), .pin17(led_val[10]), .pin18(led_val[9]),
    .pin19(led_val[8]), .pin20(1'b1));
  _74541 _74541_4 (
    .pin1(WRITE_lhs), .pin2(delay_9_out), .pin3(delay_10_out), .pin4(delay_11_out), .pin5(delay_12_out),
    .pin6(delay_13_out), .pin7(delay_14_out), .pin8(delay_15_out), .pin9(delay_16_out), .pin10(1'b0),
    .pin11(lhs_out[7]), .pin12(lhs_out[6]), .pin13(lhs_out[5]), .pin14(lhs_out[4]), .pin15(lhs_out[3]),
    .pin16(lhs_out[2]), .pin17(lhs_out[1]), .pin18(lhs_out[0]), .pin19(1'b0), .pin20(1'b1));
  _7432 _7432_1 (
    .pin1(READ_lhs), .pin2(READ_rhs), .pin3(_7432_1_pin3), .pin4(WRITE_lhs), .pin5(WRITE_rhs),
    .pin6(_7432_1_pin6), .pin7(1'b0), .pin9(1'b0), .pin10(1'b0), .pin11(display), .pin12(_7432_1_pin6),
    .pin13(_7432_1_pin3), .pin14(1'b1));  // open: pin8
  // Pins of 1 and 16 bits meet at pc
  // Pins of 1 and 8 bits meet at rhs_out
  // Pins of 1 and 8 bits meet at lhs_out

  // Other names for the same wires on the sheet: LHS_0 = lhs[0]; LHS_1 = lhs[1]; LHS_2 = lhs[2]; LHS_3 = lhs[3];
  //   LHS_4 = lhs[4]; LHS_5 = lhs[5]; LHS_6 = lhs[6]; LHS_7 = lhs[7]; lo_0 = lhs_out[0]; lo_1 = lhs_out[1];
  //   lo_2 = lhs_out[2]; lo_3 = lhs_out[3]; lo_4 = lhs_out[4]; lo_5 = lhs_out[5]; lo_6 = lhs_out[6];
  //   lo_7 = lhs_out[7]; _2OUT_0 = pc[0]; lr0 = pc[0]; _2OUT_1 = pc[1]; lr1 = pc[1]; _2OUT_2 = pc[2]; lr2 = pc[2];
  //   _2OUT_3 = pc[3]; lr3 = pc[3]; _2OUT_4 = pc[4]; lr4 = pc[4]; _2OUT_5 = pc[5]; lr5 = pc[5]; _2OUT_6 = pc[6];
  //   lr6 = pc[6]; _2OUT_7 = pc[7]; lr7 = pc[7]; _2OUT_8 = pc[8]; lr8 = pc[8]; _2OUT_9 = pc[9]; lr9 = pc[9];
  //   _2OUT_10 = pc[10]; lr10 = pc[10]; _2OUT_11 = pc[11]; lr11 = pc[11]; _2OUT_12 = pc[12]; lr12 = pc[12];
  //   _2OUT_13 = pc[13]; lr13 = pc[13]; _2OUT_14 = pc[14]; lr14 = pc[14]; _2OUT_15 = pc[15]; lr15 = pc[15];
  //   Q0 = led_val[0]; Q1 = led_val[1]; Q2 = led_val[2]; Q3 = led_val[3]; Q4 = led_val[4]; Q5 = led_val[5];
  //   Q6 = led_val[6]; Q7 = led_val[7]; Q8 = led_val[8]; Q9 = led_val[9]; Q10 = led_val[10]; Q11 = led_val[11];
  //   Q12 = led_val[12]; Q13 = led_val[13]; Q14 = led_val[14]; Q15 = led_val[15]; READ_1 = READ_lhs;
  //   READ_2 = READ_rhs; RHS_0 = rhs[0]; RHS_1 = rhs[1]; RHS_2 = rhs[2]; RHS_3 = rhs[3]; RHS_4 = rhs[4];
  //   RHS_5 = rhs[5]; RHS_6 = rhs[6]; RHS_7 = rhs[7]; ro_0 = rhs_out[0]; ro_1 = rhs_out[1]; ro_2 = rhs_out[2];
  //   ro_3 = rhs_out[3]; ro_4 = rhs_out[4]; ro_5 = rhs_out[5]; ro_6 = rhs_out[6]; ro_7 = rhs_out[7]
endmodule
