// Digital circuit timer_control_unit.dig as structural Verilog
module timer_control_unit (
  input  clk,
  input  reset,
  input  end_seq,
  output [2:0] out,
  output led_end
);

  wire Q0, Q1, Q2;

  not not_1 (led_end, end_seq);
  _74163 _74163_1 (
    .pin1(reset), .pin2(clk), .pin3(1'b0), .pin4(1'b0), .pin5(1'b0), .pin6(1'b0), .pin7(1'b1), .pin8(1'b0),
    .pin9(end_seq), .pin10(1'b1), .pin12(Q2), .pin13(Q1), .pin14(Q0), .pin16(1'b1));  // open: pin11, pin15
  Delay #(.Bits(3)) delay_1 (.in({Q2, Q1, Q0}), .out(out));
endmodule
